// Logisim project circuit.circ as structural Verilog: 44 circuits, main circuit main
module main (
  input  BINAIRE,
  input  in_2,
  input  in_3,
  input  in_4
);

  wire clock_1_out, cycle_2_q0, cycle_2_q1, cycle_2_q2, cycle_2_q3, cycle_3_q0, cycle_3_q1, cycle_3_q2,
       cycle_3_q3, cycle_4_q0, cycle_4_q1, cycle_4_q2, cycle_4_q3, cycle_5_q0, cycle_5_q1, cycle_5_q2,
       cycle_5_q3, cycle_6_q0, cycle_6_q1, cycle_6_q2, cycle_6_q3, cycle_q0, cycle_q1, cycle_q2, cycle_q3,
       tickblocker_1_s, tickblocker_2_s, tickblocker_3_s, tickblocker_4_s, tickblocker_5_s, tickblocker_6_s;
  wire [3:0] affres_mult_1_a0, affres_mult_1_a4, comparateur_1_s3, comparateur_2_s3, comparateur_3_s3,
       comparateur_4_s3, comparateur_5_s3, comparateur_6_s3, register_1_q, register_2_q, register_3_q,
       register_4_q, register_5_q, register_6_q, transco_nb_cyclic_1421_7seg_1_a0,
       transco_nb_cyclic_1421_7seg_1_a4, transco_nb_cyclic_1421_7seg_2_a0, transco_nb_cyclic_1421_7seg_2_a4,
       transco_nb_cyclic_1421_7seg_3_a0, transco_nb_cyclic_1421_7seg_3_a4, transco_nb_cyclic_1421_7seg_4_a0,
       transco_nb_cyclic_1421_7seg_4_a4, transco_nb_cyclic_1421_7seg_5_a0, transco_nb_cyclic_1421_7seg_5_a4,
       transco_nb_cyclic_1421_7seg_6_a0, transco_nb_cyclic_1421_7seg_6_a4;

  Clock clock_1 (.out(clock_1_out));
  cycle cycle (.in_1(clock_1_out), .Q3(cycle_q3), .Q2(cycle_q2), .Q1(cycle_q1), .Q0(cycle_q0));
  cycle cycle_2 (.in_1(clock_1_out), .Q3(cycle_2_q3), .Q2(cycle_2_q2), .Q1(cycle_2_q1), .Q0(cycle_2_q0));
  cycle cycle_3 (.in_1(clock_1_out), .Q3(cycle_3_q3), .Q2(cycle_3_q2), .Q1(cycle_3_q1), .Q0(cycle_3_q0));
  cycle cycle_4 (.in_1(clock_1_out), .Q3(cycle_4_q3), .Q2(cycle_4_q2), .Q1(cycle_4_q1), .Q0(cycle_4_q0));
  cycle cycle_5 (.in_1(clock_1_out), .Q3(cycle_5_q3), .Q2(cycle_5_q2), .Q1(cycle_5_q1), .Q0(cycle_5_q0));
  cycle cycle_6 (.in_1(clock_1_out), .Q3(cycle_6_q3), .Q2(cycle_6_q2), .Q1(cycle_6_q1), .Q0(cycle_6_q0));
  LED led_1 (.in(comparateur_1_s3[3]));
  LED led_2 (.in(comparateur_1_s3[2]));
  LED led_3 (.in(comparateur_1_s3[1]));
  comparateur_1 comparateur_1 (
    .Q3m(cycle_q3), .Q2m(cycle_q2), .Q1m(cycle_q1), .Q0m(cycle_q0), .Q3c(BINAIRE), .Q2c(in_2), .Q1c(in_3),
    .Q0c(in_4), .S3(comparateur_1_s3[3]), .S2(comparateur_1_s3[2]), .S1(comparateur_1_s3[1]),
    .S0(comparateur_1_s3[0]));
  LED led_4 (.in(comparateur_2_s3[2]));
  LED led_5 (.in(comparateur_2_s3[3]));
  comparateur_2 comparateur_2 (
    .Q3m(BINAIRE), .Q2m(in_2), .Q1m(in_3), .Q0m(in_4), .Q3c(cycle_2_q3), .Q2c(cycle_2_q2), .Q1c(cycle_2_q1),
    .Q0c(cycle_2_q0), .S3(comparateur_2_s3[3]), .S2(comparateur_2_s3[2]), .S1(comparateur_2_s3[1]),
    .S0(comparateur_2_s3[0]));
  LED led_6 (.in(comparateur_3_s3[3]));
  comparateur_3 comparateur_3 (
    .Q3m(BINAIRE), .Q2m(in_2), .Q1m(in_3), .Q0m(in_4), .Q3c(cycle_3_q3), .Q2c(cycle_3_q2), .Q1c(cycle_3_q1),
    .Q0c(cycle_3_q0), .S3(comparateur_3_s3[3]), .S2(comparateur_3_s3[2]), .S1(comparateur_3_s3[1]),
    .S0(comparateur_3_s3[0]));
  LED led_7 (.in(comparateur_4_s3[3]));
  comparateur_4 comparateur_4 (
    .Q3m(BINAIRE), .Q2m(in_2), .Q1m(in_3), .Q0m(in_4), .Q3c(cycle_4_q3), .Q2c(cycle_4_q2), .Q1c(cycle_4_q1),
    .Q0c(cycle_4_q0), .S3(comparateur_4_s3[3]), .S2(comparateur_4_s3[2]), .S1(comparateur_4_s3[1]),
    .S0(comparateur_4_s3[0]));
  comparateur_5 comparateur_5 (
    .Q3m(BINAIRE), .Q2m(in_2), .Q1m(in_3), .Q0m(in_4), .Q3c(cycle_5_q3), .Q2c(cycle_5_q2), .Q1c(cycle_5_q1),
    .Q0c(cycle_5_q0), .S3(comparateur_5_s3[3]), .S2(comparateur_5_s3[2]), .S1(comparateur_5_s3[1]),
    .S0(comparateur_5_s3[0]));
  comparateur_6 comparateur_6 (
    .Q3m(BINAIRE), .Q2m(in_2), .Q1m(in_3), .Q0m(in_4), .Q3c(cycle_6_q3), .Q2c(cycle_6_q2), .Q1c(cycle_6_q1),
    .Q0c(cycle_6_q0), .S3(comparateur_6_s3[3]), .S2(comparateur_6_s3[2]), .S1(comparateur_6_s3[1]),
    .S0(comparateur_6_s3[0]));
  LED led_8 (.in(comparateur_1_s3[1]));
  LED led_9 (.in(comparateur_2_s3[1]));
  LED led_10 (.in(comparateur_2_s3[0]));
  LED led_11 (.in(comparateur_3_s3[0]));
  LED led_12 (.in(comparateur_3_s3[2]));
  LED led_13 (.in(comparateur_3_s3[1]));
  LED led_14 (.in(comparateur_4_s3[2]));
  LED led_15 (.in(comparateur_4_s3[1]));
  LED led_16 (.in(comparateur_4_s3[0]));
  LED led_17 (.in(comparateur_5_s3[2]));
  LED led_18 (.in(comparateur_5_s3[1]));
  LED led_19 (.in(comparateur_5_s3[3]));
  LED led_20 (.in(comparateur_5_s3[0]));
  LED led_21 (.in(comparateur_6_s3[1]));
  LED led_22 (.in(comparateur_6_s3[2]));
  LED led_23 (.in(comparateur_6_s3[3]));
  LED led_24 (.in(comparateur_6_s3[0]));
  Register #(.width(4)) register_1 (
    .D({comparateur_1_s3[0], comparateur_1_s3[1], comparateur_1_s3[2], comparateur_1_s3[3]}),
    .Q(register_1_q), .clk(tickblocker_1_s));  // open: en, clr
  tickblocker tickblocker_1 (
    .Q3(comparateur_1_s3[0]), .Q2(comparateur_1_s3[1]), .Q1(comparateur_1_s3[2]), .Q0(comparateur_1_s3[3]),
    .S(tickblocker_1_s));
  Register #(.width(4)) register_2 (
    .D({comparateur_2_s3[0], comparateur_2_s3[1], comparateur_2_s3[2], comparateur_2_s3[3]}),
    .Q(register_2_q), .clk(tickblocker_2_s));  // open: en, clr
  tickblocker tickblocker_2 (
    .Q3(comparateur_2_s3[0]), .Q2(comparateur_2_s3[1]), .Q1(comparateur_2_s3[2]), .Q0(comparateur_2_s3[3]),
    .S(tickblocker_2_s));
  Register #(.width(4)) register_3 (
    .D({comparateur_3_s3[0], comparateur_3_s3[1], comparateur_3_s3[2], comparateur_3_s3[3]}),
    .Q(register_3_q), .clk(tickblocker_3_s));  // open: en, clr
  tickblocker tickblocker_3 (
    .Q3(comparateur_3_s3[0]), .Q2(comparateur_3_s3[1]), .Q1(comparateur_3_s3[2]), .Q0(comparateur_3_s3[3]),
    .S(tickblocker_3_s));
  Register #(.width(4)) register_4 (
    .D({comparateur_4_s3[0], comparateur_4_s3[1], comparateur_4_s3[2], comparateur_4_s3[3]}),
    .Q(register_4_q), .clk(tickblocker_4_s));  // open: en, clr
  tickblocker tickblocker_4 (
    .Q3(comparateur_4_s3[0]), .Q2(comparateur_4_s3[1]), .Q1(comparateur_4_s3[2]), .Q0(comparateur_4_s3[3]),
    .S(tickblocker_4_s));
  Register #(.width(4)) register_5 (
    .D({comparateur_5_s3[0], comparateur_5_s3[1], comparateur_5_s3[2], comparateur_5_s3[3]}),
    .Q(register_5_q), .clk(tickblocker_5_s));  // open: en, clr
  tickblocker tickblocker_5 (
    .Q3(comparateur_5_s3[0]), .Q2(comparateur_5_s3[1]), .Q1(comparateur_5_s3[2]), .Q0(comparateur_5_s3[3]),
    .S(tickblocker_5_s));
  Register #(.width(4)) register_6 (
    .D({comparateur_6_s3[0], comparateur_6_s3[1], comparateur_6_s3[2], comparateur_6_s3[3]}),
    .Q(register_6_q), .clk(tickblocker_6_s));  // open: en, clr
  tickblocker tickblocker_6 (
    .Q3(comparateur_6_s3[0]), .Q2(comparateur_6_s3[1]), .Q1(comparateur_6_s3[2]), .Q0(comparateur_6_s3[3]),
    .S(tickblocker_6_s));
  transco_nb_cyclic_1421_7seg transco_nb_cyclic_1421_7seg_1 (
    .b3(register_1_q[0]), .b2(register_1_q[1]), .b1(register_1_q[2]), .b0(register_1_q[3]),
    .A7(transco_nb_cyclic_1421_7seg_1_a4[3]), .A6(transco_nb_cyclic_1421_7seg_1_a4[2]),
    .A5(transco_nb_cyclic_1421_7seg_1_a4[1]), .A4(transco_nb_cyclic_1421_7seg_1_a4[0]),
    .A3(transco_nb_cyclic_1421_7seg_1_a0[3]), .A2(transco_nb_cyclic_1421_7seg_1_a0[2]),
    .A1(transco_nb_cyclic_1421_7seg_1_a0[1]), .A0(transco_nb_cyclic_1421_7seg_1_a0[0]));
  transco_nb_cyclic_1421_7seg transco_nb_cyclic_1421_7seg_2 (
    .b3(register_2_q[0]), .b2(register_2_q[1]), .b1(register_2_q[2]), .b0(register_2_q[3]),
    .A7(transco_nb_cyclic_1421_7seg_2_a4[3]), .A6(transco_nb_cyclic_1421_7seg_2_a4[2]),
    .A5(transco_nb_cyclic_1421_7seg_2_a4[1]), .A4(transco_nb_cyclic_1421_7seg_2_a4[0]),
    .A3(transco_nb_cyclic_1421_7seg_2_a0[3]), .A2(transco_nb_cyclic_1421_7seg_2_a0[2]),
    .A1(transco_nb_cyclic_1421_7seg_2_a0[1]), .A0(transco_nb_cyclic_1421_7seg_2_a0[0]));
  transco_nb_cyclic_1421_7seg transco_nb_cyclic_1421_7seg_3 (
    .b3(register_3_q[0]), .b2(register_3_q[1]), .b1(register_3_q[2]), .b0(register_3_q[3]),
    .A7(transco_nb_cyclic_1421_7seg_3_a4[3]), .A6(transco_nb_cyclic_1421_7seg_3_a4[2]),
    .A5(transco_nb_cyclic_1421_7seg_3_a4[1]), .A4(transco_nb_cyclic_1421_7seg_3_a4[0]),
    .A3(transco_nb_cyclic_1421_7seg_3_a0[3]), .A2(transco_nb_cyclic_1421_7seg_3_a0[2]),
    .A1(transco_nb_cyclic_1421_7seg_3_a0[1]), .A0(transco_nb_cyclic_1421_7seg_3_a0[0]));
  transco_nb_cyclic_1421_7seg transco_nb_cyclic_1421_7seg_4 (
    .b3(register_4_q[0]), .b2(register_4_q[1]), .b1(register_4_q[2]), .b0(register_4_q[3]),
    .A7(transco_nb_cyclic_1421_7seg_4_a4[3]), .A6(transco_nb_cyclic_1421_7seg_4_a4[2]),
    .A5(transco_nb_cyclic_1421_7seg_4_a4[1]), .A4(transco_nb_cyclic_1421_7seg_4_a4[0]),
    .A3(transco_nb_cyclic_1421_7seg_4_a0[3]), .A2(transco_nb_cyclic_1421_7seg_4_a0[2]),
    .A1(transco_nb_cyclic_1421_7seg_4_a0[1]), .A0(transco_nb_cyclic_1421_7seg_4_a0[0]));
  transco_nb_cyclic_1421_7seg transco_nb_cyclic_1421_7seg_5 (
    .b3(register_5_q[0]), .b2(register_5_q[1]), .b1(register_5_q[2]), .b0(register_5_q[3]),
    .A7(transco_nb_cyclic_1421_7seg_5_a4[3]), .A6(transco_nb_cyclic_1421_7seg_5_a4[2]),
    .A5(transco_nb_cyclic_1421_7seg_5_a4[1]), .A4(transco_nb_cyclic_1421_7seg_5_a4[0]),
    .A3(transco_nb_cyclic_1421_7seg_5_a0[3]), .A2(transco_nb_cyclic_1421_7seg_5_a0[2]),
    .A1(transco_nb_cyclic_1421_7seg_5_a0[1]), .A0(transco_nb_cyclic_1421_7seg_5_a0[0]));
  transco_nb_cyclic_1421_7seg transco_nb_cyclic_1421_7seg_6 (
    .b3(register_6_q[0]), .b2(register_6_q[1]), .b1(register_6_q[2]), .b0(register_6_q[3]),
    .A7(transco_nb_cyclic_1421_7seg_6_a4[3]), .A6(transco_nb_cyclic_1421_7seg_6_a4[2]),
    .A5(transco_nb_cyclic_1421_7seg_6_a4[1]), .A4(transco_nb_cyclic_1421_7seg_6_a4[0]),
    .A3(transco_nb_cyclic_1421_7seg_6_a0[3]), .A2(transco_nb_cyclic_1421_7seg_6_a0[2]),
    .A1(transco_nb_cyclic_1421_7seg_6_a0[1]), .A0(transco_nb_cyclic_1421_7seg_6_a0[0]));
  _7_Segment_Display u_7_segment_display_1 (
    .g(transco_nb_cyclic_1421_7seg_1_a0[0]), .f(transco_nb_cyclic_1421_7seg_1_a0[1]),
    .a(transco_nb_cyclic_1421_7seg_1_a0[2]), .b(transco_nb_cyclic_1421_7seg_1_a0[3]),
    .e(transco_nb_cyclic_1421_7seg_1_a4[0]), .d(transco_nb_cyclic_1421_7seg_1_a4[1]),
    .c(transco_nb_cyclic_1421_7seg_1_a4[2]), .dp(transco_nb_cyclic_1421_7seg_1_a4[3]));
  _7_Segment_Display u_7_segment_display_2 (
    .g(transco_nb_cyclic_1421_7seg_2_a0[0]), .f(transco_nb_cyclic_1421_7seg_2_a0[1]),
    .a(transco_nb_cyclic_1421_7seg_2_a0[2]), .b(transco_nb_cyclic_1421_7seg_2_a0[3]),
    .e(transco_nb_cyclic_1421_7seg_2_a4[0]), .d(transco_nb_cyclic_1421_7seg_2_a4[1]),
    .c(transco_nb_cyclic_1421_7seg_2_a4[2]), .dp(transco_nb_cyclic_1421_7seg_2_a4[3]));
  _7_Segment_Display u_7_segment_display_3 (
    .g(transco_nb_cyclic_1421_7seg_3_a0[0]), .f(transco_nb_cyclic_1421_7seg_3_a0[1]),
    .a(transco_nb_cyclic_1421_7seg_3_a0[2]), .b(transco_nb_cyclic_1421_7seg_3_a0[3]),
    .e(transco_nb_cyclic_1421_7seg_3_a4[0]), .d(transco_nb_cyclic_1421_7seg_3_a4[1]),
    .c(transco_nb_cyclic_1421_7seg_3_a4[2]), .dp(transco_nb_cyclic_1421_7seg_3_a4[3]));
  _7_Segment_Display u_7_segment_display_4 (
    .g(transco_nb_cyclic_1421_7seg_4_a0[0]), .f(transco_nb_cyclic_1421_7seg_4_a0[1]),
    .a(transco_nb_cyclic_1421_7seg_4_a0[2]), .b(transco_nb_cyclic_1421_7seg_4_a0[3]),
    .e(transco_nb_cyclic_1421_7seg_4_a4[0]), .d(transco_nb_cyclic_1421_7seg_4_a4[1]),
    .c(transco_nb_cyclic_1421_7seg_4_a4[2]), .dp(transco_nb_cyclic_1421_7seg_4_a4[3]));
  _7_Segment_Display u_7_segment_display_5 (
    .g(transco_nb_cyclic_1421_7seg_5_a0[0]), .f(transco_nb_cyclic_1421_7seg_5_a0[1]),
    .a(transco_nb_cyclic_1421_7seg_5_a0[2]), .b(transco_nb_cyclic_1421_7seg_5_a0[3]),
    .e(transco_nb_cyclic_1421_7seg_5_a4[0]), .d(transco_nb_cyclic_1421_7seg_5_a4[1]),
    .c(transco_nb_cyclic_1421_7seg_5_a4[2]), .dp(transco_nb_cyclic_1421_7seg_5_a4[3]));
  affres_mult affres_mult_1 (
    .A(BINAIRE), .B(in_2), .C(in_3), .D(in_4), .a7(affres_mult_1_a4[3]), .a6(affres_mult_1_a4[2]),
    .a5(affres_mult_1_a4[1]), .a4(affres_mult_1_a4[0]), .a3(affres_mult_1_a0[3]), .a2(affres_mult_1_a0[2]),
    .a1(affres_mult_1_a0[1]), .a0(affres_mult_1_a0[0]));
  _7_Segment_Display u_7_segment_display_6 (
    .g(affres_mult_1_a0[0]), .f(affres_mult_1_a0[1]), .a(affres_mult_1_a0[2]), .b(affres_mult_1_a0[3]),
    .e(affres_mult_1_a4[0]), .d(affres_mult_1_a4[1]), .c(affres_mult_1_a4[2]), .dp(affres_mult_1_a4[3]));
  _7_Segment_Display u_7_segment_display_7 (
    .g(transco_nb_cyclic_1421_7seg_6_a0[0]), .f(transco_nb_cyclic_1421_7seg_6_a0[1]),
    .a(transco_nb_cyclic_1421_7seg_6_a0[2]), .b(transco_nb_cyclic_1421_7seg_6_a0[3]),
    .e(transco_nb_cyclic_1421_7seg_6_a4[0]), .d(transco_nb_cyclic_1421_7seg_6_a4[1]),
    .c(transco_nb_cyclic_1421_7seg_6_a4[2]), .dp(transco_nb_cyclic_1421_7seg_6_a4[3]));

  // Notes on the sheet:
  //   MULTIPLICATEUR
  //   NOMBRE CYCLIQUE
endmodule

module transco_hexa_aff (
  input  A,
  input  B,
  input  C,
  input  D,
  output A7,
  output A6,
  output A5,
  output A4,
  output A3,
  output A2,
  output A1,
  output A0,
  output P
);

  wire and_1_out, and_2_out, and_3_out, and_4_out, and_5_out, and_6_out, and_7_out, and_8_out, and_9_out,
       and_10_out, and_11_out, and_12_out, and_13_out, and_14_out, and_15_out, and_16_out, and_17_out,
       and_18_out, and_19_out, and_20_out, and_21_out, and_22_out, and_23_out, and_24_out, and_25_out,
       and_26_out, and_27_out, and_28_out, and_29_out, and_30_out, and_31_out, and_32_out, and_33_out,
       and_34_out, and_35_out, and_36_out, and_37_out, and_38_out, and_39_out, and_40_out, and_41_out,
       not_1_out, not_2_out, not_3_out, not_4_out, not_5_out, not_6_out, not_7_out, not_8_out, not_9_out,
       not_10_out, not_11_out, not_12_out, not_13_out, not_14_out, not_15_out, not_16_out, not_17_out,
       not_18_out, not_19_out, not_20_out, not_21_out, not_22_out, not_23_out, not_24_out, not_25_out,
       not_26_out, not_27_out, not_28_out, not_29_out, not_30_out, not_31_out, not_32_out, not_33_out,
       not_34_out, not_35_out, not_36_out, not_37_out, not_38_out, not_39_out, not_40_out, not_41_out,
       not_42_out, not_43_out, not_44_out, not_45_out, not_46_out, not_47_out, not_48_out, not_49_out,
       not_50_out, not_51_out, not_52_out;

  and and_1 (and_1_out, A, not_1_out);
  not not_1 (not_1_out, C);
  and and_2 (and_2_out, A, not_2_out);
  not not_2 (not_2_out, D);
  not not_3 (not_3_out, C);
  and and_3 (and_3_out, not_3_out, D);
  not not_4 (not_4_out, A);
  and and_4 (and_4_out, not_4_out, B, not_5_out);
  not not_5 (not_5_out, C);
  not not_6 (not_6_out, A);
  and and_5 (and_5_out, not_6_out, B, D);
  and and_6 (and_6_out, A, not_7_out, not_8_out);
  not not_7 (not_7_out, B);
  not not_8 (not_8_out, C);
  and and_7 (and_7_out, A, C, not_9_out);
  not not_9 (not_9_out, D);
  not not_10 (not_10_out, A);
  not not_11 (not_11_out, B);
  and and_8 (and_8_out, not_10_out, not_11_out, not_12_out);
  not not_12 (not_12_out, D);
  not not_13 (not_13_out, A);
  and and_9 (and_9_out, not_13_out, C, not_14_out);
  not not_14 (not_14_out, D);
  not not_15 (not_15_out, B);
  and and_10 (and_10_out, not_15_out, C);
  and and_11 (and_11_out, B, not_16_out, D);
  not not_16 (not_16_out, C);
  and and_12 (and_12_out, A, D);
  and and_13 (and_13_out, A, B, not_17_out);
  not not_17 (not_17_out, C);
  not not_18 (not_18_out, A);
  not not_19 (not_19_out, B);
  and and_14 (and_14_out, not_18_out, not_19_out, not_20_out);
  not not_20 (not_20_out, D);
  not not_21 (not_21_out, A);
  and and_15 (and_15_out, not_21_out, C, not_22_out);
  not not_22 (not_22_out, D);
  not not_23 (not_23_out, B);
  and and_16 (and_16_out, not_23_out, C, D);
  and and_17 (and_17_out, A, B, not_24_out);
  not not_24 (not_24_out, C);
  and and_18 (and_18_out, A, B, D);
  not not_25 (not_25_out, A);
  not not_26 (not_26_out, B);
  not not_27 (not_27_out, C);
  not not_28 (not_28_out, B);
  not not_29 (not_29_out, D);
  not not_30 (not_30_out, C);
  not not_31 (not_31_out, D);
  not not_32 (not_32_out, A);
  not not_33 (not_33_out, D);
  not not_34 (not_34_out, A);
  not not_35 (not_35_out, B);
  and and_19 (and_19_out, not_34_out, not_35_out, not_36_out);
  not not_36 (not_36_out, D);
  not not_37 (not_37_out, A);
  and and_20 (and_20_out, not_37_out, C);
  not not_38 (not_38_out, B);
  and and_21 (and_21_out, not_38_out, C);
  and and_22 (and_22_out, B, D);
  and and_23 (and_23_out, A, D);
  and and_24 (and_24_out, A, B, not_39_out);
  not not_39 (not_39_out, C);
  not not_40 (not_40_out, A);
  and and_25 (and_25_out, not_40_out, not_41_out, not_42_out);
  not not_41 (not_41_out, B);
  not not_42 (not_42_out, C);
  not not_43 (not_43_out, B);
  and and_26 (and_26_out, not_43_out, D);
  not not_44 (not_44_out, C);
  and and_27 (and_27_out, not_44_out, D);
  and and_28 (and_28_out, B, C, not_45_out);
  not not_45 (not_45_out, D);
  and and_29 (and_29_out, A, D);
  not not_46 (not_46_out, A);
  and and_30 (and_30_out, not_46_out, not_47_out);
  not not_47 (not_47_out, B);
  not not_48 (not_48_out, C);
  and and_31 (and_31_out, not_48_out, D);
  not not_49 (not_49_out, B);
  and and_32 (and_32_out, not_49_out, C);
  and and_33 (and_33_out, C, not_50_out);
  not not_50 (not_50_out, D);
  and and_34 (and_34_out, A, B);
  and and_35 (and_35_out, A, not_51_out);
  not not_51 (not_51_out, C);
  and and_36 (and_36_out, A, not_52_out);
  not not_52 (not_52_out, D);
  or or_1 (A7, and_1_out, and_2_out);
  or or_2 (A6, and_3_out, and_4_out, and_5_out, and_6_out, and_7_out);
  or or_3 (A4, and_14_out, and_15_out, and_16_out, and_17_out, and_18_out);
  and and_37 (and_37_out, not_25_out, not_26_out, not_27_out, D);
  and and_38 (and_38_out, not_28_out, C, not_29_out);
  and and_39 (and_39_out, B, not_30_out, not_31_out);
  and and_40 (and_40_out, not_32_out, B, C, D);
  and and_41 (and_41_out, A, not_33_out);
  or or_4 (A1, and_25_out, and_26_out, and_27_out, and_28_out, and_29_out);
  or or_5 (A0, and_30_out, and_31_out, and_32_out, and_33_out, and_34_out);
  or or_6 (P, and_35_out, and_36_out);
  or or_7 (A5, and_8_out, and_9_out, and_10_out, and_11_out, and_12_out, and_13_out);
  or or_8 (A3, and_37_out, and_38_out, and_39_out, and_40_out, and_41_out);
  or or_9 (A2, and_19_out, and_20_out, and_21_out, and_22_out, and_23_out, and_24_out);
endmodule

module test_transco_hexa_aff (
  input  in_1,
  input  in_2,
  input  in_3,
  input  in_4
);

  wire transco_hexa_aff_1_a0, transco_hexa_aff_1_a1, transco_hexa_aff_1_a2, transco_hexa_aff_1_a3,
       transco_hexa_aff_1_a4, transco_hexa_aff_1_a5, transco_hexa_aff_1_a6, transco_hexa_aff_1_a7;

  LED led_1 (.in(in_1));
  LED led_2 (.in(in_4));
  LED led_3 (.in(in_3));
  LED led_4 (.in(in_2));
  transco_hexa_aff transco_hexa_aff_1 (
    .A(in_1), .B(in_2), .C(in_3), .D(in_4), .A7(transco_hexa_aff_1_a7), .A6(transco_hexa_aff_1_a6),
    .A5(transco_hexa_aff_1_a5), .A4(transco_hexa_aff_1_a4), .A3(transco_hexa_aff_1_a3),
    .A2(transco_hexa_aff_1_a2), .A1(transco_hexa_aff_1_a1), .A0(transco_hexa_aff_1_a0));  // open: P
  _7_Segment_Display u_7_segment_display_1 (
    .g(transco_hexa_aff_1_a0), .f(transco_hexa_aff_1_a1), .a(transco_hexa_aff_1_a2),
    .b(transco_hexa_aff_1_a3), .e(transco_hexa_aff_1_a4), .d(transco_hexa_aff_1_a5),
    .c(transco_hexa_aff_1_a6), .dp(transco_hexa_aff_1_a7));
endmodule

// transco
module transco_nb_cyclic_1421_7seg (
  input  b3,
  input  b2,
  input  b1,
  input  b0,
  output A7,
  output A6,
  output A5,
  output A4,
  output A3,
  output A2,
  output A1,
  output A0
);

  wire and_1_out, and_2_out, and_3_out, and_4_out, and_5_out, and_6_out, and_7_out, and_8_out, and_9_out,
       and_10_out, and_11_out, and_12_out, and_13_out, and_14_out, and_15_out, and_16_out, and_17_out,
       and_18_out, and_19_out, and_20_out, and_21_out, and_22_out, and_23_out, and_24_out, and_25_out,
       and_26_out, and_27_out, and_28_out, and_29_out, and_30_out, and_31_out, and_32_out, and_33_out,
       and_34_out, not_1_out, not_2_out, not_3_out, not_4_out, not_5_out, not_6_out, not_7_out, not_8_out,
       not_9_out, not_10_out, not_11_out, not_12_out, not_13_out, not_14_out, not_15_out, not_16_out,
       not_17_out, not_18_out, not_19_out, not_20_out, not_21_out, not_22_out, not_23_out, not_24_out,
       not_25_out, not_26_out, not_27_out, not_28_out, not_29_out, not_30_out, not_31_out, not_32_out,
       not_33_out, not_34_out;

  and and_1 (and_1_out, b3, not_1_out);
  not not_1 (not_1_out, b1);
  and and_2 (and_2_out, b3, not_2_out);
  not not_2 (not_2_out, b0);
  not not_3 (not_3_out, b1);
  and and_3 (and_3_out, not_3_out, b0);
  not not_4 (not_4_out, b3);
  and and_4 (and_4_out, not_4_out, b2, not_5_out);
  not not_5 (not_5_out, b1);
  and and_5 (and_5_out, b2, b0);
  and and_6 (and_6_out, b3, not_6_out, not_7_out);
  not not_6 (not_6_out, b2);
  not not_7 (not_7_out, b0);
  and and_7 (and_7_out, b3, b1, not_8_out);
  not not_8 (not_8_out, b0);
  not not_9 (not_9_out, b3);
  and and_8 (and_8_out, not_9_out, b1, not_10_out);
  not not_10 (not_10_out, b0);
  not not_11 (not_11_out, b2);
  and and_9 (and_9_out, not_11_out, b1);
  not not_12 (not_12_out, b1);
  and and_10 (and_10_out, b2, not_12_out, b0);
  and and_11 (and_11_out, b3, b0);
  and and_12 (and_12_out, b3, b2, not_13_out);
  not not_13 (not_13_out, b1);
  not not_14 (not_14_out, b3);
  and and_13 (and_13_out, not_14_out, b1, not_15_out);
  not not_15 (not_15_out, b0);
  not not_16 (not_16_out, b2);
  and and_14 (and_14_out, not_16_out, b1, b0);
  and and_15 (and_15_out, b3, b2, not_17_out);
  not not_17 (not_17_out, b1);
  and and_16 (and_16_out, b3, b2, b0);
  not not_18 (not_18_out, b3);
  not not_19 (not_19_out, b2);
  not not_20 (not_20_out, b1);
  not not_21 (not_21_out, b2);
  not not_22 (not_22_out, b0);
  not not_23 (not_23_out, b1);
  not not_24 (not_24_out, b0);
  not not_25 (not_25_out, b0);
  not not_26 (not_26_out, b3);
  and and_17 (and_17_out, not_26_out, b1);
  not not_27 (not_27_out, b2);
  and and_18 (and_18_out, not_27_out, b1);
  and and_19 (and_19_out, b2, b0);
  and and_20 (and_20_out, b3, b0);
  and and_21 (and_21_out, b3, b2, not_28_out);
  not not_28 (not_28_out, b1);
  not not_29 (not_29_out, b2);
  and and_22 (and_22_out, not_29_out, b0);
  not not_30 (not_30_out, b1);
  and and_23 (and_23_out, not_30_out, b0);
  and and_24 (and_24_out, b2, b1, not_31_out);
  not not_31 (not_31_out, b0);
  and and_25 (and_25_out, b3, b0);
  not not_32 (not_32_out, b1);
  and and_26 (and_26_out, not_32_out, b0);
  not not_33 (not_33_out, b2);
  and and_27 (and_27_out, not_33_out, b1);
  and and_28 (and_28_out, b1, not_34_out);
  not not_34 (not_34_out, b0);
  and and_29 (and_29_out, b3, b2);
  or or_1 (A7, and_1_out, and_2_out);
  or or_2 (A6, and_3_out, and_4_out, and_5_out, and_6_out, and_7_out);
  or or_3 (A5, and_8_out, and_9_out, and_10_out, and_11_out, and_12_out);
  or or_4 (A4, and_13_out, and_14_out, and_15_out, and_16_out);
  and and_30 (and_30_out, not_18_out, not_19_out, not_20_out, b0);
  and and_31 (and_31_out, not_21_out, b1, not_22_out);
  and and_32 (and_32_out, b2, not_23_out, not_24_out);
  and and_33 (and_33_out, b2, b1, b0);
  and and_34 (and_34_out, b3, not_25_out);
  or or_5 (A2, and_17_out, and_18_out, and_19_out, and_20_out, and_21_out);
  or or_6 (A1, and_22_out, and_23_out, and_24_out, and_25_out);
  or or_7 (A0, and_26_out, and_27_out, and_28_out, and_29_out);
  or or_8 (A3, and_30_out, and_31_out, and_32_out, and_33_out, and_34_out);
endmodule

module test_transco_nb_cyclic_1421_7seg (
  input  in_1,
  input  in_2,
  input  in_3,
  input  in_4
);

  wire transco_nb_cyclic_1421_7seg_1_a0, transco_nb_cyclic_1421_7seg_1_a1, transco_nb_cyclic_1421_7seg_1_a2,
       transco_nb_cyclic_1421_7seg_1_a3, transco_nb_cyclic_1421_7seg_1_a4, transco_nb_cyclic_1421_7seg_1_a5,
       transco_nb_cyclic_1421_7seg_1_a6, transco_nb_cyclic_1421_7seg_1_a7;

  transco_nb_cyclic_1421_7seg transco_nb_cyclic_1421_7seg_1 (
    .b3(in_1), .b2(in_2), .b1(in_3), .b0(in_4), .A7(transco_nb_cyclic_1421_7seg_1_a7),
    .A6(transco_nb_cyclic_1421_7seg_1_a6), .A5(transco_nb_cyclic_1421_7seg_1_a5),
    .A4(transco_nb_cyclic_1421_7seg_1_a4), .A3(transco_nb_cyclic_1421_7seg_1_a3),
    .A2(transco_nb_cyclic_1421_7seg_1_a2), .A1(transco_nb_cyclic_1421_7seg_1_a1),
    .A0(transco_nb_cyclic_1421_7seg_1_a0));
  _7_Segment_Display u_7_segment_display_1 (
    .g(transco_nb_cyclic_1421_7seg_1_a0), .f(transco_nb_cyclic_1421_7seg_1_a1),
    .a(transco_nb_cyclic_1421_7seg_1_a2), .b(transco_nb_cyclic_1421_7seg_1_a3),
    .e(transco_nb_cyclic_1421_7seg_1_a4), .d(transco_nb_cyclic_1421_7seg_1_a5),
    .c(transco_nb_cyclic_1421_7seg_1_a6), .dp(transco_nb_cyclic_1421_7seg_1_a7));
endmodule

// af 1
module affiche_cyclique_1 (
  input  A,
  output b3,
  output b2,
  output b1,
  output b0
);


  assign b0 = 1'b0;
  assign b1 = 1'b0;
  assign b2 = A;
  assign b3 = 1'b0;
endmodule

// af 4
module affiche_cyclique_4 (
  input  A,
  output b3,
  output b2,
  output b1,
  output b0
);


  assign b0 = A;
  assign b1 = 1'b0;
  assign b2 = 1'b0;
  assign b3 = 1'b0;
endmodule

// af 2
module affiche_cyclique_2 (
  input  A,
  output b3,
  output b2,
  output b1,
  output b0
);


  assign b0 = 1'b0;
  assign b1 = A;
  assign b2 = 1'b0;
  assign b3 = 1'b0;
endmodule

// af 8
module affiche_cyclique_8 (
  input  A,
  output b3,
  output b2,
  output b1,
  output b0
);


  assign b0 = A;
  assign b1 = A;
  assign b2 = A;
  assign b3 = A;
endmodule

// af 5
module affiche_cyclique_5 (
  input  A,
  output b3,
  output b2,
  output b1,
  output b0
);


  assign b0 = A;
  assign b1 = 1'b0;
  assign b2 = A;
  assign b3 = 1'b0;
endmodule

// af 7
module affiche_cyclique_7 (
  input  A,
  output b3,
  output b2,
  output b1,
  output b0
);


  assign b0 = A;
  assign b1 = A;
  assign b2 = A;
  assign b3 = 1'b0;
endmodule

module affiche_cyclique7seg (
  input  in_1
);

  wire affiche_cyclique_1_1_b0, affiche_cyclique_1_1_b1, affiche_cyclique_1_1_b2, affiche_cyclique_1_1_b3,
       affiche_cyclique_2_1_b0, affiche_cyclique_2_1_b1, affiche_cyclique_2_1_b2, affiche_cyclique_2_1_b3,
       affiche_cyclique_4_1_b0, affiche_cyclique_4_1_b1, affiche_cyclique_4_1_b2, affiche_cyclique_4_1_b3,
       affiche_cyclique_5_1_b0, affiche_cyclique_5_1_b1, affiche_cyclique_5_1_b2, affiche_cyclique_5_1_b3,
       affiche_cyclique_7_1_b0, affiche_cyclique_7_1_b1, affiche_cyclique_7_1_b2, affiche_cyclique_7_1_b3,
       affiche_cyclique_8_1_b0, affiche_cyclique_8_1_b1, affiche_cyclique_8_1_b2, affiche_cyclique_8_1_b3,
       transco_nb_cyclic_1421_7seg_1_a0, transco_nb_cyclic_1421_7seg_1_a1, transco_nb_cyclic_1421_7seg_1_a2,
       transco_nb_cyclic_1421_7seg_1_a3, transco_nb_cyclic_1421_7seg_1_a4, transco_nb_cyclic_1421_7seg_1_a5,
       transco_nb_cyclic_1421_7seg_1_a6, transco_nb_cyclic_1421_7seg_1_a7, transco_nb_cyclic_1421_7seg_2_a0,
       transco_nb_cyclic_1421_7seg_2_a1, transco_nb_cyclic_1421_7seg_2_a2, transco_nb_cyclic_1421_7seg_2_a3,
       transco_nb_cyclic_1421_7seg_2_a4, transco_nb_cyclic_1421_7seg_2_a5, transco_nb_cyclic_1421_7seg_2_a6,
       transco_nb_cyclic_1421_7seg_2_a7, transco_nb_cyclic_1421_7seg_3_a0, transco_nb_cyclic_1421_7seg_3_a1,
       transco_nb_cyclic_1421_7seg_3_a2, transco_nb_cyclic_1421_7seg_3_a3, transco_nb_cyclic_1421_7seg_3_a4,
       transco_nb_cyclic_1421_7seg_3_a5, transco_nb_cyclic_1421_7seg_3_a6, transco_nb_cyclic_1421_7seg_3_a7,
       transco_nb_cyclic_1421_7seg_4_a0, transco_nb_cyclic_1421_7seg_4_a1, transco_nb_cyclic_1421_7seg_4_a2,
       transco_nb_cyclic_1421_7seg_4_a3, transco_nb_cyclic_1421_7seg_4_a4, transco_nb_cyclic_1421_7seg_4_a5,
       transco_nb_cyclic_1421_7seg_4_a6, transco_nb_cyclic_1421_7seg_4_a7, transco_nb_cyclic_1421_7seg_5_a0,
       transco_nb_cyclic_1421_7seg_5_a1, transco_nb_cyclic_1421_7seg_5_a2, transco_nb_cyclic_1421_7seg_5_a3,
       transco_nb_cyclic_1421_7seg_5_a4, transco_nb_cyclic_1421_7seg_5_a5, transco_nb_cyclic_1421_7seg_5_a6,
       transco_nb_cyclic_1421_7seg_5_a7, transco_nb_cyclic_1421_7seg_6_a0, transco_nb_cyclic_1421_7seg_6_a1,
       transco_nb_cyclic_1421_7seg_6_a2, transco_nb_cyclic_1421_7seg_6_a3, transco_nb_cyclic_1421_7seg_6_a4,
       transco_nb_cyclic_1421_7seg_6_a5, transco_nb_cyclic_1421_7seg_6_a6, transco_nb_cyclic_1421_7seg_6_a7;

  affiche_cyclique_1 affiche_cyclique_1_1 (
    .A(in_1), .b3(affiche_cyclique_1_1_b3), .b2(affiche_cyclique_1_1_b2), .b1(affiche_cyclique_1_1_b1),
    .b0(affiche_cyclique_1_1_b0));
  affiche_cyclique_4 affiche_cyclique_4_1 (
    .A(in_1), .b3(affiche_cyclique_4_1_b3), .b2(affiche_cyclique_4_1_b2), .b1(affiche_cyclique_4_1_b1),
    .b0(affiche_cyclique_4_1_b0));
  affiche_cyclique_2 affiche_cyclique_2_1 (
    .A(in_1), .b3(affiche_cyclique_2_1_b3), .b2(affiche_cyclique_2_1_b2), .b1(affiche_cyclique_2_1_b1),
    .b0(affiche_cyclique_2_1_b0));
  affiche_cyclique_8 affiche_cyclique_8_1 (
    .A(in_1), .b3(affiche_cyclique_8_1_b3), .b2(affiche_cyclique_8_1_b2), .b1(affiche_cyclique_8_1_b1),
    .b0(affiche_cyclique_8_1_b0));
  affiche_cyclique_5 affiche_cyclique_5_1 (
    .A(in_1), .b3(affiche_cyclique_5_1_b3), .b2(affiche_cyclique_5_1_b2), .b1(affiche_cyclique_5_1_b1),
    .b0(affiche_cyclique_5_1_b0));
  affiche_cyclique_7 affiche_cyclique_7_1 (
    .A(in_1), .b3(affiche_cyclique_7_1_b3), .b2(affiche_cyclique_7_1_b2), .b1(affiche_cyclique_7_1_b1),
    .b0(affiche_cyclique_7_1_b0));
  transco_nb_cyclic_1421_7seg transco_nb_cyclic_1421_7seg_1 (
    .b3(affiche_cyclique_1_1_b3), .b2(affiche_cyclique_1_1_b2), .b1(affiche_cyclique_1_1_b1),
    .b0(affiche_cyclique_1_1_b0), .A7(transco_nb_cyclic_1421_7seg_1_a7),
    .A6(transco_nb_cyclic_1421_7seg_1_a6), .A5(transco_nb_cyclic_1421_7seg_1_a5),
    .A4(transco_nb_cyclic_1421_7seg_1_a4), .A3(transco_nb_cyclic_1421_7seg_1_a3),
    .A2(transco_nb_cyclic_1421_7seg_1_a2), .A1(transco_nb_cyclic_1421_7seg_1_a1),
    .A0(transco_nb_cyclic_1421_7seg_1_a0));
  transco_nb_cyclic_1421_7seg transco_nb_cyclic_1421_7seg_2 (
    .b3(affiche_cyclique_2_1_b3), .b2(affiche_cyclique_2_1_b2), .b1(affiche_cyclique_2_1_b1),
    .b0(affiche_cyclique_2_1_b0), .A7(transco_nb_cyclic_1421_7seg_2_a7),
    .A6(transco_nb_cyclic_1421_7seg_2_a6), .A5(transco_nb_cyclic_1421_7seg_2_a5),
    .A4(transco_nb_cyclic_1421_7seg_2_a4), .A3(transco_nb_cyclic_1421_7seg_2_a3),
    .A2(transco_nb_cyclic_1421_7seg_2_a2), .A1(transco_nb_cyclic_1421_7seg_2_a1),
    .A0(transco_nb_cyclic_1421_7seg_2_a0));
  transco_nb_cyclic_1421_7seg transco_nb_cyclic_1421_7seg_3 (
    .b3(affiche_cyclique_5_1_b3), .b2(affiche_cyclique_5_1_b2), .b1(affiche_cyclique_5_1_b1),
    .b0(affiche_cyclique_5_1_b0), .A7(transco_nb_cyclic_1421_7seg_3_a7),
    .A6(transco_nb_cyclic_1421_7seg_3_a6), .A5(transco_nb_cyclic_1421_7seg_3_a5),
    .A4(transco_nb_cyclic_1421_7seg_3_a4), .A3(transco_nb_cyclic_1421_7seg_3_a3),
    .A2(transco_nb_cyclic_1421_7seg_3_a2), .A1(transco_nb_cyclic_1421_7seg_3_a1),
    .A0(transco_nb_cyclic_1421_7seg_3_a0));
  _7_Segment_Display u_7_segment_display_1 (
    .g(transco_nb_cyclic_1421_7seg_1_a0), .f(transco_nb_cyclic_1421_7seg_1_a1),
    .a(transco_nb_cyclic_1421_7seg_1_a2), .b(transco_nb_cyclic_1421_7seg_1_a3),
    .e(transco_nb_cyclic_1421_7seg_1_a4), .d(transco_nb_cyclic_1421_7seg_1_a5),
    .c(transco_nb_cyclic_1421_7seg_1_a6), .dp(transco_nb_cyclic_1421_7seg_1_a7));
  _7_Segment_Display u_7_segment_display_2 (
    .g(transco_nb_cyclic_1421_7seg_3_a0), .f(transco_nb_cyclic_1421_7seg_3_a1),
    .a(transco_nb_cyclic_1421_7seg_3_a2), .b(transco_nb_cyclic_1421_7seg_3_a3),
    .e(transco_nb_cyclic_1421_7seg_3_a4), .d(transco_nb_cyclic_1421_7seg_3_a5),
    .c(transco_nb_cyclic_1421_7seg_3_a6), .dp(transco_nb_cyclic_1421_7seg_3_a7));
  _7_Segment_Display u_7_segment_display_3 (
    .g(transco_nb_cyclic_1421_7seg_2_a0), .f(transco_nb_cyclic_1421_7seg_2_a1),
    .a(transco_nb_cyclic_1421_7seg_2_a2), .b(transco_nb_cyclic_1421_7seg_2_a3),
    .e(transco_nb_cyclic_1421_7seg_2_a4), .d(transco_nb_cyclic_1421_7seg_2_a5),
    .c(transco_nb_cyclic_1421_7seg_2_a6), .dp(transco_nb_cyclic_1421_7seg_2_a7));
  transco_nb_cyclic_1421_7seg transco_nb_cyclic_1421_7seg_4 (
    .b3(affiche_cyclique_4_1_b3), .b2(affiche_cyclique_4_1_b2), .b1(affiche_cyclique_4_1_b1),
    .b0(affiche_cyclique_4_1_b0), .A7(transco_nb_cyclic_1421_7seg_4_a7),
    .A6(transco_nb_cyclic_1421_7seg_4_a6), .A5(transco_nb_cyclic_1421_7seg_4_a5),
    .A4(transco_nb_cyclic_1421_7seg_4_a4), .A3(transco_nb_cyclic_1421_7seg_4_a3),
    .A2(transco_nb_cyclic_1421_7seg_4_a2), .A1(transco_nb_cyclic_1421_7seg_4_a1),
    .A0(transco_nb_cyclic_1421_7seg_4_a0));
  transco_nb_cyclic_1421_7seg transco_nb_cyclic_1421_7seg_5 (
    .b3(affiche_cyclique_8_1_b3), .b2(affiche_cyclique_8_1_b2), .b1(affiche_cyclique_8_1_b1),
    .b0(affiche_cyclique_8_1_b0), .A7(transco_nb_cyclic_1421_7seg_5_a7),
    .A6(transco_nb_cyclic_1421_7seg_5_a6), .A5(transco_nb_cyclic_1421_7seg_5_a5),
    .A4(transco_nb_cyclic_1421_7seg_5_a4), .A3(transco_nb_cyclic_1421_7seg_5_a3),
    .A2(transco_nb_cyclic_1421_7seg_5_a2), .A1(transco_nb_cyclic_1421_7seg_5_a1),
    .A0(transco_nb_cyclic_1421_7seg_5_a0));
  transco_nb_cyclic_1421_7seg transco_nb_cyclic_1421_7seg_6 (
    .b3(affiche_cyclique_7_1_b3), .b2(affiche_cyclique_7_1_b2), .b1(affiche_cyclique_7_1_b1),
    .b0(affiche_cyclique_7_1_b0), .A7(transco_nb_cyclic_1421_7seg_6_a7),
    .A6(transco_nb_cyclic_1421_7seg_6_a6), .A5(transco_nb_cyclic_1421_7seg_6_a5),
    .A4(transco_nb_cyclic_1421_7seg_6_a4), .A3(transco_nb_cyclic_1421_7seg_6_a3),
    .A2(transco_nb_cyclic_1421_7seg_6_a2), .A1(transco_nb_cyclic_1421_7seg_6_a1),
    .A0(transco_nb_cyclic_1421_7seg_6_a0));
  _7_Segment_Display u_7_segment_display_4 (
    .g(transco_nb_cyclic_1421_7seg_4_a0), .f(transco_nb_cyclic_1421_7seg_4_a1),
    .a(transco_nb_cyclic_1421_7seg_4_a2), .b(transco_nb_cyclic_1421_7seg_4_a3),
    .e(transco_nb_cyclic_1421_7seg_4_a4), .d(transco_nb_cyclic_1421_7seg_4_a5),
    .c(transco_nb_cyclic_1421_7seg_4_a6), .dp(transco_nb_cyclic_1421_7seg_4_a7));
  _7_Segment_Display u_7_segment_display_5 (
    .g(transco_nb_cyclic_1421_7seg_5_a0), .f(transco_nb_cyclic_1421_7seg_5_a1),
    .a(transco_nb_cyclic_1421_7seg_5_a2), .b(transco_nb_cyclic_1421_7seg_5_a3),
    .e(transco_nb_cyclic_1421_7seg_5_a4), .d(transco_nb_cyclic_1421_7seg_5_a5),
    .c(transco_nb_cyclic_1421_7seg_5_a6), .dp(transco_nb_cyclic_1421_7seg_5_a7));
  _7_Segment_Display u_7_segment_display_6 (
    .g(transco_nb_cyclic_1421_7seg_6_a0), .f(transco_nb_cyclic_1421_7seg_6_a1),
    .a(transco_nb_cyclic_1421_7seg_6_a2), .b(transco_nb_cyclic_1421_7seg_6_a3),
    .e(transco_nb_cyclic_1421_7seg_6_a4), .d(transco_nb_cyclic_1421_7seg_6_a5),
    .c(transco_nb_cyclic_1421_7seg_6_a6), .dp(transco_nb_cyclic_1421_7seg_6_a7));
endmodule

module aff_res_mult (
  input  in_1,
  input  in_2,
  input  in_3,
  input  in_4
);

  wire aff_1_res_mult_1_a0, aff_1_res_mult_1_a1, aff_1_res_mult_1_a2, aff_1_res_mult_1_a3,
       aff_1_res_mult_1_a4, aff_1_res_mult_1_a5, aff_1_res_mult_1_a6, aff_1_res_mult_1_a7,
       aff_2_res_mult_1_a0, aff_2_res_mult_1_a1, aff_2_res_mult_1_a2, aff_2_res_mult_1_a3,
       aff_2_res_mult_1_a4, aff_2_res_mult_1_a5, aff_2_res_mult_1_a6, aff_2_res_mult_1_a7,
       aff_3_res_mult_1_a0, aff_3_res_mult_1_a1, aff_3_res_mult_1_a2, aff_3_res_mult_1_a3,
       aff_3_res_mult_1_a4, aff_3_res_mult_1_a5, aff_3_res_mult_1_a6, aff_3_res_mult_1_a7,
       aff_4_res_mult_1_a0, aff_4_res_mult_1_a1, aff_4_res_mult_1_a2, aff_4_res_mult_1_a3,
       aff_4_res_mult_1_a4, aff_4_res_mult_1_a5, aff_4_res_mult_1_a6, aff_4_res_mult_1_a7,
       aff_5_res_mult_1_a0, aff_5_res_mult_1_a1, aff_5_res_mult_1_a2, aff_5_res_mult_1_a3,
       aff_5_res_mult_1_a4, aff_5_res_mult_1_a5, aff_5_res_mult_1_a6, aff_5_res_mult_1_a7,
       aff_6_res_mult_1_a0, aff_6_res_mult_1_a1, aff_6_res_mult_1_a2, aff_6_res_mult_1_a3,
       aff_6_res_mult_1_a4, aff_6_res_mult_1_a5, aff_6_res_mult_1_a6, aff_6_res_mult_1_a7,
       transco_nb_cyclic_1421_7seg_1_a0, transco_nb_cyclic_1421_7seg_1_a1, transco_nb_cyclic_1421_7seg_1_a2,
       transco_nb_cyclic_1421_7seg_1_a3, transco_nb_cyclic_1421_7seg_1_a4, transco_nb_cyclic_1421_7seg_1_a5,
       transco_nb_cyclic_1421_7seg_1_a6, transco_nb_cyclic_1421_7seg_1_a7;

  transco_nb_cyclic_1421_7seg transco_nb_cyclic_1421_7seg_1 (
    .b3(in_1), .b2(in_2), .b1(in_3), .b0(in_4), .A7(transco_nb_cyclic_1421_7seg_1_a7),
    .A6(transco_nb_cyclic_1421_7seg_1_a6), .A5(transco_nb_cyclic_1421_7seg_1_a5),
    .A4(transco_nb_cyclic_1421_7seg_1_a4), .A3(transco_nb_cyclic_1421_7seg_1_a3),
    .A2(transco_nb_cyclic_1421_7seg_1_a2), .A1(transco_nb_cyclic_1421_7seg_1_a1),
    .A0(transco_nb_cyclic_1421_7seg_1_a0));
  aff_1_res_mult aff_1_res_mult_1 (
    .A(in_1), .B(in_2), .C(in_3), .D(in_4), .a7(aff_1_res_mult_1_a7), .a6(aff_1_res_mult_1_a6),
    .a5(aff_1_res_mult_1_a5), .a4(aff_1_res_mult_1_a4), .a3(aff_1_res_mult_1_a3), .a2(aff_1_res_mult_1_a2),
    .a1(aff_1_res_mult_1_a1), .a0(aff_1_res_mult_1_a0));
  aff_2_res_mult aff_2_res_mult_1 (
    .A(in_1), .B(in_2), .C(in_3), .D(in_4), .a7(aff_2_res_mult_1_a7), .a6(aff_2_res_mult_1_a6),
    .a5(aff_2_res_mult_1_a5), .a4(aff_2_res_mult_1_a4), .a3(aff_2_res_mult_1_a3), .a2(aff_2_res_mult_1_a2),
    .a1(aff_2_res_mult_1_a1), .a0(aff_2_res_mult_1_a0));
  aff_3_res_mult aff_3_res_mult_1 (
    .A(in_1), .B(in_2), .C(in_3), .D(in_4), .a7(aff_3_res_mult_1_a7), .a6(aff_3_res_mult_1_a6),
    .a5(aff_3_res_mult_1_a5), .a4(aff_3_res_mult_1_a4), .a3(aff_3_res_mult_1_a3), .a2(aff_3_res_mult_1_a2),
    .a1(aff_3_res_mult_1_a1), .a0(aff_3_res_mult_1_a0));
  aff_4_res_mult aff_4_res_mult_1 (
    .A(in_1), .B(in_2), .C(in_3), .D(in_4), .a7(aff_4_res_mult_1_a7), .a6(aff_4_res_mult_1_a6),
    .a5(aff_4_res_mult_1_a5), .a4(aff_4_res_mult_1_a4), .a3(aff_4_res_mult_1_a3), .a2(aff_4_res_mult_1_a2),
    .a1(aff_4_res_mult_1_a1), .a0(aff_4_res_mult_1_a0));
  aff_5_res_mult aff_5_res_mult_1 (
    .A(in_1), .B(in_2), .C(in_3), .D(in_4), .a7(aff_5_res_mult_1_a7), .a6(aff_5_res_mult_1_a6),
    .a5(aff_5_res_mult_1_a5), .a4(aff_5_res_mult_1_a4), .a3(aff_5_res_mult_1_a3), .a2(aff_5_res_mult_1_a2),
    .a1(aff_5_res_mult_1_a1), .a0(aff_5_res_mult_1_a0));
  aff_6_res_mult aff_6_res_mult_1 (
    .A(in_1), .B(in_2), .C(in_3), .D(in_4), .a7(aff_6_res_mult_1_a7), .a6(aff_6_res_mult_1_a6),
    .a5(aff_6_res_mult_1_a5), .a4(aff_6_res_mult_1_a4), .a3(aff_6_res_mult_1_a3), .a2(aff_6_res_mult_1_a2),
    .a1(aff_6_res_mult_1_a1), .a0(aff_6_res_mult_1_a0));
  _7_Segment_Display u_7_segment_display_1 (
    .g(transco_nb_cyclic_1421_7seg_1_a0), .f(transco_nb_cyclic_1421_7seg_1_a1),
    .a(transco_nb_cyclic_1421_7seg_1_a2), .b(transco_nb_cyclic_1421_7seg_1_a3),
    .e(transco_nb_cyclic_1421_7seg_1_a4), .d(transco_nb_cyclic_1421_7seg_1_a5),
    .c(transco_nb_cyclic_1421_7seg_1_a6), .dp(transco_nb_cyclic_1421_7seg_1_a7));
  _7_Segment_Display u_7_segment_display_2 (
    .g(aff_1_res_mult_1_a0), .f(aff_1_res_mult_1_a1), .a(aff_1_res_mult_1_a2), .b(aff_1_res_mult_1_a3),
    .e(aff_1_res_mult_1_a4), .d(aff_1_res_mult_1_a5), .c(aff_1_res_mult_1_a6), .dp(aff_1_res_mult_1_a7));
  _7_Segment_Display u_7_segment_display_3 (
    .g(aff_2_res_mult_1_a0), .f(aff_2_res_mult_1_a1), .a(aff_2_res_mult_1_a2), .b(aff_2_res_mult_1_a3),
    .e(aff_2_res_mult_1_a4), .d(aff_2_res_mult_1_a5), .c(aff_2_res_mult_1_a6), .dp(aff_2_res_mult_1_a7));
  _7_Segment_Display u_7_segment_display_4 (
    .g(aff_3_res_mult_1_a0), .f(aff_3_res_mult_1_a1), .a(aff_3_res_mult_1_a2), .b(aff_3_res_mult_1_a3),
    .e(aff_3_res_mult_1_a4), .d(aff_3_res_mult_1_a5), .c(aff_3_res_mult_1_a6), .dp(aff_3_res_mult_1_a7));
  _7_Segment_Display u_7_segment_display_5 (
    .g(aff_4_res_mult_1_a0), .f(aff_4_res_mult_1_a1), .a(aff_4_res_mult_1_a2), .b(aff_4_res_mult_1_a3),
    .e(aff_4_res_mult_1_a4), .d(aff_4_res_mult_1_a5), .c(aff_4_res_mult_1_a6), .dp(aff_4_res_mult_1_a7));
  _7_Segment_Display u_7_segment_display_6 (
    .g(aff_5_res_mult_1_a0), .f(aff_5_res_mult_1_a1), .a(aff_5_res_mult_1_a2), .b(aff_5_res_mult_1_a3),
    .e(aff_5_res_mult_1_a4), .d(aff_5_res_mult_1_a5), .c(aff_5_res_mult_1_a6), .dp(aff_5_res_mult_1_a7));
  _7_Segment_Display u_7_segment_display_7 (
    .g(aff_6_res_mult_1_a0), .f(aff_6_res_mult_1_a1), .a(aff_6_res_mult_1_a2), .b(aff_6_res_mult_1_a3),
    .e(aff_6_res_mult_1_a4), .d(aff_6_res_mult_1_a5), .c(aff_6_res_mult_1_a6), .dp(aff_6_res_mult_1_a7));

  // Notes on the sheet:
  //   Multiplicateur
endmodule

// aff_1
module aff_1_res_mult (
  input  A,
  input  B,
  input  C,
  input  D,
  output a7,
  output a6,
  output a5,
  output a4,
  output a3,
  output a2,
  output a1,
  output a0
);

  wire and_1_out, and_2_out, and_3_out, and_4_out, and_5_out, and_6_out, and_7_out, and_8_out, and_9_out,
       not_1_out, not_2_out, not_3_out, not_4_out, not_5_out, not_6_out, not_7_out, not_8_out, not_9_out,
       not_10_out, not_11_out, not_12_out, not_13_out;

  not not_1 (not_1_out, B);
  and and_1 (and_1_out, A, not_1_out, not_2_out);
  not not_2 (not_2_out, C);
  not not_3 (not_3_out, C);
  and and_2 (and_2_out, A, not_3_out, D);
  and and_3 (and_3_out, A, C, not_4_out);
  not not_4 (not_4_out, D);
  not not_5 (not_5_out, A);
  and and_4 (and_4_out, C, D);
  not not_6 (not_6_out, A);
  and and_5 (and_5_out, C, D);
  and and_6 (and_6_out, B, not_7_out);
  not not_7 (not_7_out, C);
  not not_8 (not_8_out, B);
  and and_7 (and_7_out, A, not_8_out, not_9_out);
  not not_9 (not_9_out, D);
  and and_8 (and_8_out, A, not_10_out);
  not not_10 (not_10_out, C);
  not not_11 (not_11_out, A);
  or or_1 (a2, not_11_out, D, B);
  not not_12 (not_12_out, A);
  and and_9 (and_9_out, B, D);
  not not_13 (not_13_out, A);
  or or_2 (a0, not_13_out, C, B);
  or or_3 (a6, and_1_out, and_2_out, and_3_out);
  or or_4 (a5, not_5_out, and_4_out, B);
  or or_5 (a4, not_6_out, and_5_out, and_6_out);
  or or_6 (a3, and_7_out, and_8_out);
  or or_7 (a1, not_12_out, C, and_9_out);

  assign a7 = 1'b0;
endmodule

// aff_2
module aff_2_res_mult (
  input  A,
  input  B,
  input  C,
  input  D,
  output a7,
  output a6,
  output a5,
  output a4,
  output a3,
  output a2,
  output a1,
  output a0
);

  wire and_1_out, and_2_out, and_3_out, and_4_out, and_5_out, and_6_out, and_7_out, and_8_out, and_9_out,
       and_10_out, and_11_out, and_12_out, and_13_out, and_14_out, and_15_out, and_16_out, not_1_out,
       not_2_out, not_3_out, not_4_out, not_5_out, not_6_out, not_7_out, not_8_out, not_9_out, not_10_out,
       not_11_out, not_12_out, not_13_out, not_14_out, not_15_out, not_16_out, not_17_out, not_18_out,
       not_19_out, not_20_out, not_21_out;

  and and_1 (and_1_out, A, not_1_out);
  not not_1 (not_1_out, C);
  and and_2 (and_2_out, A, B, not_2_out);
  not not_2 (not_2_out, D);
  not not_3 (not_3_out, A);
  not not_4 (not_4_out, B);
  and and_3 (and_3_out, not_4_out, C);
  and and_4 (and_4_out, B, not_5_out);
  not not_5 (not_5_out, C);
  and and_5 (and_5_out, B, D);
  not not_6 (not_6_out, A);
  not not_7 (not_7_out, B);
  and and_6 (and_6_out, not_7_out, C);
  and and_7 (and_7_out, C, D);
  not not_8 (not_8_out, C);
  and and_8 (and_8_out, B, not_8_out, not_9_out);
  not not_9 (not_9_out, D);
  not not_10 (not_10_out, B);
  and and_9 (and_9_out, A, not_10_out, not_11_out);
  not not_11 (not_11_out, C);
  and and_10 (and_10_out, A, not_12_out);
  not not_12 (not_12_out, D);
  not not_13 (not_13_out, A);
  or or_1 (a2, not_13_out, C, B);
  not not_14 (not_14_out, A);
  not not_15 (not_15_out, C);
  and and_11 (and_11_out, not_15_out, not_16_out);
  not not_16 (not_16_out, D);
  and and_12 (and_12_out, C, D);
  and and_13 (and_13_out, B, not_17_out);
  not not_17 (not_17_out, C);
  not not_18 (not_18_out, A);
  not not_19 (not_19_out, B);
  and and_14 (and_14_out, not_19_out, not_20_out);
  not not_20 (not_20_out, D);
  and and_15 (and_15_out, C, D);
  and and_16 (and_16_out, B, not_21_out);
  not not_21 (not_21_out, C);
  or or_2 (a6, and_1_out, and_2_out);
  or or_3 (a5, not_3_out, and_3_out, and_4_out, and_5_out);
  or or_4 (a4, not_6_out, and_6_out, and_7_out, and_8_out);
  or or_5 (a3, and_9_out, and_10_out);
  or or_6 (a1, not_14_out, and_11_out, and_12_out, and_13_out);
  or or_7 (a0, not_18_out, and_14_out, and_15_out, and_16_out);

  assign a7 = 1'b0;
endmodule

// aff_3
module aff_3_res_mult (
  input  A,
  input  B,
  input  C,
  input  D,
  output a7,
  output a6,
  output a5,
  output a4,
  output a3,
  output a2,
  output a1,
  output a0
);

  wire and_1_out, and_2_out, and_3_out, and_4_out, and_5_out, and_6_out, and_7_out, and_8_out, and_9_out,
       and_10_out, and_11_out, and_12_out, and_13_out, and_14_out, and_15_out, and_16_out, and_17_out,
       and_18_out, and_19_out, and_20_out, not_1_out, not_2_out, not_3_out, not_4_out, not_5_out, not_6_out,
       not_7_out, not_8_out, not_9_out, not_10_out, not_11_out, not_12_out, not_13_out, not_14_out,
       not_15_out, not_16_out, not_17_out, not_18_out, not_19_out, not_20_out, not_21_out, not_22_out,
       not_23_out, not_24_out, not_25_out, not_26_out, not_27_out, not_28_out;

  not not_1 (not_1_out, C);
  and and_1 (and_1_out, A, not_1_out, D);
  and and_2 (and_2_out, A, C, not_2_out);
  not not_2 (not_2_out, D);
  and and_3 (and_3_out, A, B, not_3_out);
  not not_3 (not_3_out, C);
  not not_4 (not_4_out, A);
  not not_5 (not_5_out, B);
  and and_4 (and_4_out, not_5_out, not_6_out);
  not not_6 (not_6_out, D);
  not not_7 (not_7_out, C);
  and and_5 (and_5_out, not_7_out, not_8_out);
  not not_8 (not_8_out, D);
  and and_6 (and_6_out, C, D);
  not not_9 (not_9_out, A);
  not not_10 (not_10_out, B);
  and and_7 (and_7_out, not_10_out, not_11_out);
  not not_11 (not_11_out, D);
  and and_8 (and_8_out, C, D);
  not not_12 (not_12_out, B);
  and and_9 (and_9_out, A, not_12_out, not_13_out);
  not not_13 (not_13_out, C);
  and and_10 (and_10_out, A, not_14_out, D);
  not not_14 (not_14_out, C);
  and and_11 (and_11_out, A, C, not_15_out);
  not not_15 (not_15_out, D);
  not not_16 (not_16_out, A);
  not not_17 (not_17_out, B);
  and and_12 (and_12_out, not_17_out, not_18_out);
  not not_18 (not_18_out, D);
  and and_13 (and_13_out, C, D);
  and and_14 (and_14_out, B, not_19_out);
  not not_19 (not_19_out, C);
  not not_20 (not_20_out, A);
  not not_21 (not_21_out, B);
  and and_15 (and_15_out, not_21_out, D);
  not not_22 (not_22_out, B);
  and and_16 (and_16_out, not_22_out, C);
  and and_17 (and_17_out, C, D);
  not not_23 (not_23_out, C);
  and and_18 (and_18_out, B, not_23_out, not_24_out);
  not not_24 (not_24_out, D);
  not not_25 (not_25_out, A);
  not not_26 (not_26_out, B);
  not not_27 (not_27_out, C);
  and and_19 (and_19_out, not_27_out, not_28_out);
  not not_28 (not_28_out, D);
  and and_20 (and_20_out, C, D);
  or or_1 (a6, and_1_out, and_2_out, and_3_out);
  or or_2 (a5, not_4_out, and_4_out, and_5_out, and_6_out);
  or or_3 (a4, not_9_out, and_7_out, and_8_out);
  or or_4 (a3, and_9_out, and_10_out, and_11_out);
  or or_5 (a2, not_16_out, and_12_out, and_13_out, and_14_out);
  or or_6 (a1, not_20_out, and_15_out, and_16_out, and_17_out, and_18_out);
  or or_7 (a0, not_25_out, not_26_out, and_19_out, and_20_out);

  assign a7 = 1'b0;
endmodule

// aff_4
module aff_4_res_mult (
  input  A,
  input  B,
  input  C,
  input  D,
  output a7,
  output a6,
  output a5,
  output a4,
  output a3,
  output a2,
  output a1,
  output a0
);

  wire and_1_out, and_2_out, and_3_out, and_4_out, and_5_out, and_6_out, and_7_out, and_8_out, and_9_out,
       and_10_out, not_1_out, not_2_out, not_3_out, not_4_out, not_5_out, not_6_out, not_7_out, not_8_out,
       not_9_out, not_10_out, not_11_out, not_12_out, not_13_out, not_14_out, not_15_out, not_16_out,
       not_17_out, not_18_out;

  and and_1 (and_1_out, A, not_1_out);
  not not_1 (not_1_out, D);
  and and_2 (and_2_out, A, B, not_2_out);
  not not_2 (not_2_out, C);
  not not_3 (not_3_out, A);
  not not_4 (not_4_out, B);
  and and_3 (and_3_out, C, D);
  not not_5 (not_5_out, A);
  not not_6 (not_6_out, B);
  and and_4 (and_4_out, not_6_out, not_7_out);
  not not_7 (not_7_out, C);
  and and_5 (and_5_out, C, D);
  and and_6 (and_6_out, A, not_8_out);
  not not_8 (not_8_out, C);
  and and_7 (and_7_out, A, B, not_9_out);
  not not_9 (not_9_out, D);
  not not_10 (not_10_out, A);
  not not_11 (not_11_out, B);
  not not_12 (not_12_out, C);
  and and_8 (and_8_out, not_12_out, not_13_out);
  not not_13 (not_13_out, D);
  and and_9 (and_9_out, C, D);
  not not_14 (not_14_out, A);
  not not_15 (not_15_out, B);
  and and_10 (and_10_out, not_15_out, not_16_out);
  not not_16 (not_16_out, D);
  not not_17 (not_17_out, A);
  not not_18 (not_18_out, B);
  or or_1 (a0, not_17_out, not_18_out, C);
  or or_2 (a6, and_1_out, and_2_out);
  or or_3 (a5, not_3_out, not_4_out, and_3_out);
  or or_4 (a4, not_5_out, and_4_out, and_5_out);
  or or_5 (a3, and_6_out, and_7_out);
  or or_6 (a2, not_10_out, not_11_out, and_8_out, and_9_out);
  or or_7 (a1, not_14_out, and_10_out, C);

  assign a7 = 1'b0;
endmodule

// aff_5
module aff_5_res_mult (
  input  A,
  input  B,
  input  C,
  input  D,
  output a7,
  output a6,
  output a5,
  output a4,
  output a3,
  output a2,
  output a1,
  output a0
);

  wire and_1_out, and_2_out, and_3_out, and_4_out, and_5_out, and_6_out, and_7_out, and_8_out, and_9_out,
       and_10_out, and_11_out, and_12_out, and_13_out, not_1_out, not_2_out, not_3_out, not_4_out, not_5_out,
       not_6_out, not_7_out, not_8_out, not_9_out, not_10_out, not_11_out, not_12_out, not_13_out,
       not_14_out, not_15_out, not_16_out, not_17_out, not_18_out, not_19_out, not_20_out;

  not not_1 (not_1_out, B);
  and and_1 (and_1_out, A, not_1_out, not_2_out);
  not not_2 (not_2_out, D);
  and and_2 (and_2_out, A, not_3_out);
  not not_3 (not_3_out, C);
  not not_4 (not_4_out, A);
  not not_5 (not_5_out, B);
  and and_3 (and_3_out, not_5_out, not_6_out);
  not not_6 (not_6_out, C);
  not not_7 (not_7_out, B);
  and and_4 (and_4_out, not_7_out, D);
  and and_5 (and_5_out, B, C);
  not not_8 (not_8_out, A);
  not not_9 (not_9_out, B);
  and and_6 (and_6_out, not_9_out, D);
  and and_7 (and_7_out, B, C);
  and and_8 (and_8_out, A, not_10_out, D);
  not not_10 (not_10_out, C);
  and and_9 (and_9_out, A, C, not_11_out);
  not not_11 (not_11_out, D);
  and and_10 (and_10_out, A, B, not_12_out);
  not not_12 (not_12_out, C);
  not not_13 (not_13_out, A);
  or or_1 (a2, not_13_out, not_14_out, C);
  not not_14 (not_14_out, B);
  not not_15 (not_15_out, A);
  not not_16 (not_16_out, B);
  and and_11 (and_11_out, not_16_out, not_17_out);
  not not_17 (not_17_out, C);
  not not_18 (not_18_out, A);
  not not_19 (not_19_out, B);
  and and_12 (and_12_out, not_19_out, not_20_out);
  not not_20 (not_20_out, C);
  and and_13 (and_13_out, B, C);
  or or_2 (a6, and_1_out, and_2_out);
  or or_3 (a5, not_4_out, and_3_out, and_4_out, and_5_out);
  or or_4 (a4, not_8_out, and_6_out, and_7_out);
  or or_5 (a3, and_8_out, and_9_out, and_10_out);
  or or_6 (a1, not_15_out, and_11_out, D);
  or or_7 (a0, not_18_out, and_12_out, D, and_13_out);

  assign a7 = 1'b0;
endmodule

// aff_6
module aff_6_res_mult (
  input  A,
  input  B,
  input  C,
  input  D,
  output a7,
  output a6,
  output a5,
  output a4,
  output a3,
  output a2,
  output a1,
  output a0
);

  wire and_1_out, and_2_out, and_3_out, and_4_out, and_5_out, and_6_out, and_7_out, and_8_out, and_9_out,
       and_10_out, and_11_out, and_12_out, and_13_out, not_1_out, not_2_out, not_3_out, not_4_out, not_5_out,
       not_6_out, not_7_out, not_8_out, not_9_out, not_10_out, not_11_out, not_12_out, not_13_out, not_14_out;

  not not_1 (not_1_out, B);
  and and_1 (and_1_out, A, not_1_out, not_2_out);
  not not_2 (not_2_out, C);
  and and_2 (and_2_out, A, not_3_out);
  not not_3 (not_3_out, D);
  not not_4 (not_4_out, A);
  and and_3 (and_3_out, B, C);
  not not_5 (not_5_out, A);
  and and_4 (and_4_out, C, D);
  and and_5 (and_5_out, B, D);
  and and_6 (and_6_out, B, C);
  and and_7 (and_7_out, A, not_6_out);
  not not_6 (not_6_out, D);
  and and_8 (and_8_out, A, B, not_7_out);
  not not_7 (not_7_out, C);
  not not_8 (not_8_out, A);
  not not_9 (not_9_out, B);
  and and_9 (and_9_out, not_9_out, not_10_out);
  not not_10 (not_10_out, C);
  and and_10 (and_10_out, B, C);
  not not_11 (not_11_out, A);
  not not_12 (not_12_out, B);
  and and_11 (and_11_out, not_12_out, D);
  and and_12 (and_12_out, B, not_13_out);
  not not_13 (not_13_out, D);
  and and_13 (and_13_out, B, C);
  not not_14 (not_14_out, A);
  or or_1 (a0, not_14_out, D, B);
  or or_2 (a6, and_1_out, and_2_out);
  or or_3 (a5, not_4_out, D, and_3_out);
  or or_4 (a4, not_5_out, and_4_out, and_5_out, and_6_out);
  or or_5 (a3, and_7_out, and_8_out);
  or or_6 (a2, not_8_out, and_9_out, D, and_10_out);
  or or_7 (a1, not_11_out, and_11_out, and_12_out, and_13_out);

  assign a7 = 1'b0;
endmodule

module cycle_complet_nb_1 (
  input  in_1,
  output Q3,
  output Q2,
  output Q1,
  output Q0
);

  wire cycle_nb_1_1_j0, cycle_nb_1_1_j1, cycle_nb_1_1_j2, cycle_nb_1_1_j3, cycle_nb_1_1_k0, cycle_nb_1_1_k1,
       cycle_nb_1_1_k2, cycle_nb_1_1_k3;

  J_K_Flip_Flop J3K3 (.J(cycle_nb_1_1_j3), .clk(in_1), .K(cycle_nb_1_1_k3), .Q(Q3));  // open: Qn, preset, en, reset
  J_K_Flip_Flop J2K2 (.J(cycle_nb_1_1_j2), .clk(in_1), .K(cycle_nb_1_1_k2), .Q(Q2));  // open: Qn, preset, en, reset
  J_K_Flip_Flop J1K1 (.J(cycle_nb_1_1_j1), .clk(in_1), .K(cycle_nb_1_1_k1), .Q(Q1));  // open: Qn, preset, en, reset
  J_K_Flip_Flop J0K0 (.J(cycle_nb_1_1_j0), .clk(in_1), .K(cycle_nb_1_1_k0), .Q(Q0));  // open: Qn, preset, en, reset
  cycle_nb_1 cycle_nb_1_1 (
    .Q3(Q3), .Q2(Q2), .Q1(Q1), .Q0(Q0), .J3(cycle_nb_1_1_j3), .K3(cycle_nb_1_1_k3), .J2(cycle_nb_1_1_j2),
    .K2(cycle_nb_1_1_k2), .J1(cycle_nb_1_1_j1), .K1(cycle_nb_1_1_k1), .J0(cycle_nb_1_1_j0),
    .K0(cycle_nb_1_1_k0));
endmodule

module cycle_complet_nb_2 (
  input  in_1,
  output Q3,
  output Q2,
  output Q1,
  output Q0
);

  wire cycle_nb_2_1_j0, cycle_nb_2_1_j1, cycle_nb_2_1_j2, cycle_nb_2_1_j3, cycle_nb_2_1_k0, cycle_nb_2_1_k1,
       cycle_nb_2_1_k2, cycle_nb_2_1_k3;

  J_K_Flip_Flop J3K3 (.J(cycle_nb_2_1_j3), .clk(in_1), .K(cycle_nb_2_1_k3), .Q(Q3));  // open: Qn, preset, en, reset
  J_K_Flip_Flop J2K2 (.J(cycle_nb_2_1_j2), .clk(in_1), .K(cycle_nb_2_1_k2), .Q(Q2));  // open: Qn, preset, en, reset
  J_K_Flip_Flop J1K1 (.J(cycle_nb_2_1_j1), .clk(in_1), .K(cycle_nb_2_1_k1), .Q(Q1));  // open: Qn, preset, en, reset
  J_K_Flip_Flop J0K0 (.J(cycle_nb_2_1_j0), .clk(in_1), .K(cycle_nb_2_1_k0), .Q(Q0));  // open: Qn, preset, en, reset
  cycle_nb_2 cycle_nb_2_1 (
    .Q3(Q3), .Q2(Q2), .Q1(Q1), .Q0(Q0), .J3(cycle_nb_2_1_j3), .K3(cycle_nb_2_1_k3), .J2(cycle_nb_2_1_j2),
    .K2(cycle_nb_2_1_k2), .J1(cycle_nb_2_1_j1), .K1(cycle_nb_2_1_k1), .J0(cycle_nb_2_1_j0),
    .K0(cycle_nb_2_1_k0));
endmodule

module cycle_complet_nb_3 (
  input  in_1,
  output Q3,
  output Q2,
  output Q1,
  output Q0
);

  wire cycle_nb_3_1_j0, cycle_nb_3_1_j1, cycle_nb_3_1_j2, cycle_nb_3_1_j3, cycle_nb_3_1_k0, cycle_nb_3_1_k1,
       cycle_nb_3_1_k2, cycle_nb_3_1_k3;

  J_K_Flip_Flop J3K3 (.J(cycle_nb_3_1_j3), .clk(in_1), .K(cycle_nb_3_1_k3), .Q(Q3));  // open: Qn, preset, en, reset
  J_K_Flip_Flop J2K2 (.J(cycle_nb_3_1_j2), .clk(in_1), .K(cycle_nb_3_1_k2), .Q(Q2));  // open: Qn, preset, en, reset
  J_K_Flip_Flop J1K1 (.J(cycle_nb_3_1_j1), .clk(in_1), .K(cycle_nb_3_1_k1), .Q(Q1));  // open: Qn, preset, en, reset
  J_K_Flip_Flop J0K0 (.J(cycle_nb_3_1_j0), .clk(in_1), .K(cycle_nb_3_1_k0), .Q(Q0));  // open: Qn, preset, en, reset
  cycle_nb_3 cycle_nb_3_1 (
    .Q3(Q3), .Q2(Q2), .Q1(Q1), .Q0(Q0), .J3(cycle_nb_3_1_j3), .K3(cycle_nb_3_1_k3), .J2(cycle_nb_3_1_j2),
    .K2(cycle_nb_3_1_k2), .J1(cycle_nb_3_1_j1), .K1(cycle_nb_3_1_k1), .J0(cycle_nb_3_1_j0),
    .K0(cycle_nb_3_1_k0));
endmodule

module cycle_complet_nb_4 (
  input  in_1,
  output Q3,
  output Q2,
  output Q1,
  output Q0
);

  wire cycle_nb_4_1_j0, cycle_nb_4_1_j1, cycle_nb_4_1_j2, cycle_nb_4_1_j3, cycle_nb_4_1_k0, cycle_nb_4_1_k1,
       cycle_nb_4_1_k2, cycle_nb_4_1_k3;

  J_K_Flip_Flop J3K3 (.J(cycle_nb_4_1_j3), .clk(in_1), .K(cycle_nb_4_1_k3), .Q(Q3));  // open: Qn, preset, en, reset
  J_K_Flip_Flop J2K2 (.J(cycle_nb_4_1_j2), .clk(in_1), .K(cycle_nb_4_1_k2), .Q(Q2));  // open: Qn, preset, en, reset
  J_K_Flip_Flop J1K1 (.J(cycle_nb_4_1_j1), .clk(in_1), .K(cycle_nb_4_1_k1), .Q(Q1));  // open: Qn, preset, en, reset
  J_K_Flip_Flop J0K0 (.J(cycle_nb_4_1_j0), .clk(in_1), .K(cycle_nb_4_1_k0), .Q(Q0));  // open: Qn, preset, en, reset
  cycle_nb_4 cycle_nb_4_1 (
    .Q3(Q3), .Q2(Q2), .Q1(Q1), .Q0(Q0), .J3(cycle_nb_4_1_j3), .K3(cycle_nb_4_1_k3), .J2(cycle_nb_4_1_j2),
    .K2(cycle_nb_4_1_k2), .J1(cycle_nb_4_1_j1), .K1(cycle_nb_4_1_k1), .J0(cycle_nb_4_1_j0),
    .K0(cycle_nb_4_1_k0));
endmodule

module cycle_complet_nb_5 (
  input  in_1,
  output Q3,
  output Q2,
  output Q1,
  output Q0
);

  wire cycle_nb_5_1_j0, cycle_nb_5_1_j1, cycle_nb_5_1_j2, cycle_nb_5_1_j3, cycle_nb_5_1_k0, cycle_nb_5_1_k1,
       cycle_nb_5_1_k2, cycle_nb_5_1_k3;

  J_K_Flip_Flop J3K3 (.J(cycle_nb_5_1_j3), .clk(in_1), .K(cycle_nb_5_1_k3), .Q(Q3));  // open: Qn, preset, en, reset
  J_K_Flip_Flop J2K2 (.J(cycle_nb_5_1_j2), .clk(in_1), .K(cycle_nb_5_1_k2), .Q(Q2));  // open: Qn, preset, en, reset
  J_K_Flip_Flop J1K1 (.J(cycle_nb_5_1_j1), .clk(in_1), .K(cycle_nb_5_1_k1), .Q(Q1));  // open: Qn, preset, en, reset
  J_K_Flip_Flop J0K0 (.J(cycle_nb_5_1_j0), .clk(in_1), .K(cycle_nb_5_1_k0), .Q(Q0));  // open: Qn, preset, en, reset
  cycle_nb_5 cycle_nb_5_1 (
    .Q3(Q3), .Q2(Q2), .Q1(Q1), .Q0(Q0), .J3(cycle_nb_5_1_j3), .K3(cycle_nb_5_1_k3), .J2(cycle_nb_5_1_j2),
    .K2(cycle_nb_5_1_k2), .J1(cycle_nb_5_1_j1), .K1(cycle_nb_5_1_k1), .J0(cycle_nb_5_1_j0),
    .K0(cycle_nb_5_1_k0));
endmodule

module cycle_complet_nb_6 (
  input  in_1,
  output Q3,
  output Q2,
  output Q1,
  output Q0
);

  wire cycle_nb_6_1_j0, cycle_nb_6_1_j1, cycle_nb_6_1_j2, cycle_nb_6_1_j3, cycle_nb_6_1_k0, cycle_nb_6_1_k1,
       cycle_nb_6_1_k2, cycle_nb_6_1_k3;

  J_K_Flip_Flop J3K3 (.J(cycle_nb_6_1_j3), .clk(in_1), .K(cycle_nb_6_1_k3), .Q(Q3));  // open: Qn, preset, en, reset
  J_K_Flip_Flop J2K2 (.J(cycle_nb_6_1_j2), .clk(in_1), .K(cycle_nb_6_1_k2), .Q(Q2));  // open: Qn, preset, en, reset
  J_K_Flip_Flop J1K1 (.J(cycle_nb_6_1_j1), .clk(in_1), .K(cycle_nb_6_1_k1), .Q(Q1));  // open: Qn, preset, en, reset
  J_K_Flip_Flop J0K0 (.J(cycle_nb_6_1_j0), .clk(in_1), .K(cycle_nb_6_1_k0), .Q(Q0));  // open: Qn, preset, en, reset
  cycle_nb_6 cycle_nb_6_1 (
    .Q3(Q3), .Q2(Q2), .Q1(Q1), .Q0(Q0), .J3(cycle_nb_6_1_j3), .K3(cycle_nb_6_1_k3), .J2(cycle_nb_6_1_j2),
    .K2(cycle_nb_6_1_k2), .J1(cycle_nb_6_1_j1), .K1(cycle_nb_6_1_k1), .J0(cycle_nb_6_1_j0),
    .K0(cycle_nb_6_1_k0));
endmodule

module cycle_nb_1 (
  input  Q3,
  input  Q2,
  input  Q1,
  input  Q0,
  output J3,
  output K3,
  output J2,
  output K2,
  output J1,
  output K1,
  output J0,
  output K0
);

  wire and_1_out, and_2_out, and_3_out, and_4_out, and_5_out, and_6_out, and_7_out, and_8_out, and_9_out,
       and_10_out, and_11_out, and_12_out, and_13_out, and_14_out, and_15_out, not_1_out, not_2_out,
       not_3_out, not_4_out, not_5_out, not_6_out, not_7_out, not_8_out, not_9_out, not_10_out, not_11_out,
       not_12_out, not_13_out, not_14_out, not_15_out, not_16_out, not_17_out, not_18_out, not_19_out,
       not_20_out, not_21_out, not_22_out, not_23_out;

  not not_1 (not_1_out, Q3);
  not not_2 (not_2_out, Q2);
  not not_3 (not_3_out, Q0);
  not not_4 (not_4_out, Q3);
  not not_5 (not_5_out, Q2);
  and and_1 (and_1_out, not_4_out, not_5_out, not_6_out);
  not not_6 (not_6_out, Q0);
  not not_7 (not_7_out, Q3);
  not not_8 (not_8_out, Q1);
  and and_2 (and_2_out, not_7_out, not_8_out, Q0);
  and and_3 (and_3_out, Q2, Q1, Q0);
  not not_9 (not_9_out, Q0);
  not not_10 (not_10_out, Q2);
  and and_4 (and_4_out, not_10_out, Q1);
  and and_5 (and_5_out, Q3, not_11_out);
  not not_11 (not_11_out, Q1);
  not not_12 (not_12_out, Q0);
  not not_13 (not_13_out, Q2);
  and and_6 (and_6_out, not_13_out, Q1);
  and and_7 (and_7_out, Q3, not_14_out);
  not not_14 (not_14_out, Q1);
  not not_15 (not_15_out, Q3);
  and and_8 (and_8_out, not_15_out, not_16_out, Q0);
  not not_16 (not_16_out, Q1);
  and and_9 (and_9_out, Q2, Q1, Q0);
  not not_17 (not_17_out, Q2);
  not not_18 (not_18_out, Q1);
  and and_10 (and_10_out, not_17_out, not_18_out, not_19_out);
  not not_19 (not_19_out, Q0);
  and and_11 (and_11_out, Q1, Q0);
  and and_12 (and_12_out, Q2, Q0);
  and and_13 (and_13_out, Q2, Q1);
  or or_1 (J0, Q0, Q1, Q2, Q3);
  not not_20 (not_20_out, Q2);
  not not_21 (not_21_out, Q0);
  not not_22 (not_22_out, Q3);
  and and_14 (and_14_out, not_22_out, Q1);
  and and_15 (and_15_out, Q3, not_23_out);
  not not_23 (not_23_out, Q1);
  and and_16 (J3, not_1_out, not_2_out, Q1, not_3_out);
  or or_2 (K3, and_1_out, and_2_out, and_3_out);
  or or_3 (J2, not_9_out, and_4_out, and_5_out);
  or or_4 (K2, not_12_out, and_6_out, and_7_out);
  or or_5 (J1, and_8_out, and_9_out);
  or or_6 (K1, and_10_out, and_11_out, and_12_out, and_13_out, Q3);
  or or_7 (K0, not_20_out, not_21_out, and_14_out, and_15_out);
endmodule

module cycle_nb_2 (
  input  Q3,
  input  Q2,
  input  Q1,
  input  Q0,
  output J3,
  output K3,
  output J2,
  output K2,
  output J1,
  output K1,
  output J0,
  output K0
);

  wire and_1_out, and_2_out, and_3_out, and_4_out, and_5_out, and_6_out, and_7_out, and_8_out, and_9_out,
       not_1_out, not_2_out, not_3_out, not_4_out, not_5_out, not_6_out, not_7_out, not_8_out, not_9_out,
       not_10_out, not_11_out, not_12_out, not_13_out, not_14_out, not_15_out;

  not not_1 (not_1_out, Q2);
  and and_1 (and_1_out, not_1_out, Q1);
  not not_2 (not_2_out, Q3);
  not not_3 (not_3_out, Q1);
  and and_2 (and_2_out, not_2_out, not_3_out, not_4_out);
  not not_4 (not_4_out, Q0);
  not not_5 (not_5_out, Q0);
  not not_6 (not_6_out, Q2);
  and and_3 (and_3_out, not_6_out, Q1);
  and and_4 (and_4_out, Q3, not_7_out);
  not not_7 (not_7_out, Q1);
  not not_8 (not_8_out, Q3);
  and and_5 (and_5_out, not_8_out, not_9_out);
  not not_9 (not_9_out, Q2);
  not not_10 (not_10_out, Q3);
  and and_6 (and_6_out, not_10_out, Q0);
  and and_7 (and_7_out, Q2, Q1, Q0);
  not not_11 (not_11_out, Q1);
  or or_1 (K1, not_11_out, Q2);
  or or_2 (J0, Q0, Q1, Q2, Q3);
  not not_12 (not_12_out, Q2);
  not not_13 (not_13_out, Q0);
  not not_14 (not_14_out, Q3);
  and and_8 (and_8_out, not_14_out, Q1);
  and and_9 (and_9_out, Q3, not_15_out);
  not not_15 (not_15_out, Q1);
  or or_3 (J3, and_1_out, Q3);
  or or_4 (K3, and_2_out, Q2);
  or or_5 (K2, not_5_out, and_3_out, and_4_out);
  or or_6 (J1, and_5_out, and_6_out, and_7_out);
  or or_7 (K0, not_12_out, not_13_out, and_8_out, and_9_out);

  assign J2 = Q1;
endmodule

module cycle_nb_3 (
  input  Q3,
  input  Q2,
  input  Q1,
  input  Q0,
  output J3,
  output K3,
  output J2,
  output K2,
  output J1,
  output K1,
  output J0,
  output K0
);

  wire and_1_out, and_2_out, and_3_out, and_4_out, and_5_out, and_6_out, and_7_out, and_8_out, and_9_out,
       not_1_out, not_2_out, not_3_out, not_4_out, not_5_out, not_6_out, not_7_out, not_8_out, not_9_out,
       not_10_out, not_11_out, not_12_out, not_13_out, not_14_out, not_15_out;

  not not_1 (not_1_out, Q2);
  and and_1 (and_1_out, not_1_out, Q1);
  not not_2 (not_2_out, Q3);
  and and_2 (and_2_out, not_2_out, not_3_out, not_4_out);
  not not_3 (not_3_out, Q1);
  not not_4 (not_4_out, Q0);
  not not_5 (not_5_out, Q0);
  not not_6 (not_6_out, Q2);
  and and_3 (and_3_out, not_6_out, Q1);
  and and_4 (and_4_out, Q3, not_7_out);
  not not_7 (not_7_out, Q1);
  not not_8 (not_8_out, Q3);
  and and_5 (and_5_out, not_8_out, Q0);
  not not_9 (not_9_out, Q3);
  and and_6 (and_6_out, not_9_out, not_10_out, Q1);
  not not_10 (not_10_out, Q2);
  and and_7 (and_7_out, Q2, Q1, Q0);
  not not_11 (not_11_out, Q1);
  or or_1 (K1, not_11_out, Q2);
  not not_12 (not_12_out, Q2);
  not not_13 (not_13_out, Q0);
  not not_14 (not_14_out, Q3);
  and and_8 (and_8_out, not_14_out, Q1);
  and and_9 (and_9_out, Q3, not_15_out);
  not not_15 (not_15_out, Q1);
  or or_2 (J3, and_1_out, Q3);
  or or_3 (K3, and_2_out, Q2);
  or or_4 (K2, not_5_out, and_3_out, and_4_out);
  or or_5 (J1, and_5_out, and_6_out, and_7_out);
  or or_6 (K0, not_12_out, not_13_out, and_8_out, and_9_out);

  assign J0 = 1'b1;
  assign J2 = Q1;
endmodule

module cycle_nb_4 (
  input  Q3,
  input  Q2,
  input  Q1,
  input  Q0,
  output J3,
  output K3,
  output J2,
  output K2,
  output J1,
  output K1,
  output J0,
  output K0
);

  wire and_1_out, and_2_out, and_3_out, and_4_out, and_5_out, and_6_out, and_7_out, and_8_out, and_9_out,
       and_10_out, not_1_out, not_2_out, not_3_out, not_4_out, not_5_out, not_6_out, not_7_out, not_8_out,
       not_9_out, not_10_out, not_11_out, not_12_out, not_13_out, not_14_out, not_15_out, not_16_out,
       not_17_out, not_18_out;

  not not_1 (not_1_out, Q2);
  and and_1 (and_1_out, not_1_out, Q1);
  not not_2 (not_2_out, Q3);
  not not_3 (not_3_out, Q1);
  and and_2 (and_2_out, not_2_out, not_3_out, not_4_out);
  not not_4 (not_4_out, Q0);
  not not_5 (not_5_out, Q3);
  and and_3 (and_3_out, not_5_out, not_6_out, not_7_out);
  not not_6 (not_6_out, Q2);
  not not_7 (not_7_out, Q0);
  not not_8 (not_8_out, Q0);
  not not_9 (not_9_out, Q2);
  and and_4 (and_4_out, not_9_out, Q1);
  and and_5 (and_5_out, Q3, not_10_out);
  not not_10 (not_10_out, Q1);
  not not_11 (not_11_out, Q3);
  and and_6 (and_6_out, not_11_out, Q0);
  not not_12 (not_12_out, Q3);
  not not_13 (not_13_out, Q2);
  and and_7 (and_7_out, not_12_out, not_13_out, Q1);
  and and_8 (and_8_out, Q2, Q1, Q0);
  not not_14 (not_14_out, Q1);
  or or_1 (K1, not_14_out, Q2);
  not not_15 (not_15_out, Q2);
  not not_16 (not_16_out, Q0);
  not not_17 (not_17_out, Q3);
  and and_9 (and_9_out, not_17_out, Q1);
  and and_10 (and_10_out, Q3, not_18_out);
  not not_18 (not_18_out, Q1);
  or or_2 (J3, and_1_out, Q3);
  or or_3 (K3, and_2_out, Q2);
  or or_4 (J2, and_3_out, Q1);
  or or_5 (K2, not_8_out, and_4_out, and_5_out);
  or or_6 (J1, and_6_out, and_7_out, and_8_out);
  or or_7 (K0, not_15_out, not_16_out, and_9_out, and_10_out);

  assign J0 = 1'b1;
endmodule

module cycle_nb_5 (
  input  Q3,
  input  Q2,
  input  Q1,
  input  Q0,
  output J3,
  output K3,
  output J2,
  output K2,
  output J1,
  output K1,
  output J0,
  output K0
);

  wire and_1_out, and_2_out, and_3_out, and_4_out, and_5_out, and_6_out, and_7_out, and_8_out, and_9_out,
       and_10_out, not_1_out, not_2_out, not_3_out, not_4_out, not_5_out, not_6_out, not_7_out, not_8_out,
       not_9_out, not_10_out, not_11_out, not_12_out, not_13_out, not_14_out, not_15_out, not_16_out,
       not_17_out, not_18_out;

  not not_1 (not_1_out, Q2);
  and and_1 (and_1_out, not_1_out, Q1);
  not not_2 (not_2_out, Q3);
  and and_2 (and_2_out, not_2_out, not_3_out, not_4_out);
  not not_3 (not_3_out, Q1);
  not not_4 (not_4_out, Q0);
  not not_5 (not_5_out, Q3);
  not not_6 (not_6_out, Q2);
  and and_3 (and_3_out, not_5_out, not_6_out, not_7_out);
  not not_7 (not_7_out, Q0);
  not not_8 (not_8_out, Q0);
  not not_9 (not_9_out, Q2);
  and and_4 (and_4_out, not_9_out, Q1);
  and and_5 (and_5_out, Q3, not_10_out);
  not not_10 (not_10_out, Q1);
  not not_11 (not_11_out, Q3);
  and and_6 (and_6_out, not_11_out, not_12_out);
  not not_12 (not_12_out, Q2);
  not not_13 (not_13_out, Q3);
  and and_7 (and_7_out, not_13_out, Q0);
  and and_8 (and_8_out, Q2, Q1, Q0);
  not not_14 (not_14_out, Q1);
  or or_1 (K1, not_14_out, Q2);
  not not_15 (not_15_out, Q2);
  not not_16 (not_16_out, Q0);
  not not_17 (not_17_out, Q3);
  and and_9 (and_9_out, not_17_out, Q1);
  and and_10 (and_10_out, Q3, not_18_out);
  not not_18 (not_18_out, Q1);
  or or_2 (J3, and_1_out, Q3);
  or or_3 (K3, and_2_out, Q2);
  or or_4 (J2, and_3_out, Q1);
  or or_5 (K2, not_8_out, and_4_out, and_5_out);
  or or_6 (J1, and_6_out, and_7_out, and_8_out);
  or or_7 (K0, not_15_out, not_16_out, and_9_out, and_10_out);

  assign J0 = 1'b1;
endmodule

module cycle_nb_6 (
  input  Q3,
  input  Q2,
  input  Q1,
  input  Q0,
  output J3,
  output K3,
  output J2,
  output K2,
  output J1,
  output K1,
  output J0,
  output K0
);

  wire and_1_out, and_2_out, and_3_out, and_4_out, and_5_out, and_6_out, and_7_out, and_8_out, and_9_out,
       and_10_out, and_11_out, not_1_out, not_2_out, not_3_out, not_4_out, not_5_out, not_6_out, not_7_out,
       not_8_out, not_9_out, not_10_out, not_11_out, not_12_out, not_13_out, not_14_out, not_15_out,
       not_16_out, not_17_out, not_18_out, not_19_out, not_20_out;

  not not_1 (not_1_out, Q2);
  and and_1 (and_1_out, not_1_out, not_2_out);
  not not_2 (not_2_out, Q0);
  not not_3 (not_3_out, Q2);
  and and_2 (and_2_out, not_3_out, Q1);
  not not_4 (not_4_out, Q3);
  and and_3 (and_3_out, not_4_out, not_5_out, not_6_out);
  not not_5 (not_5_out, Q1);
  not not_6 (not_6_out, Q0);
  not not_7 (not_7_out, Q3);
  not not_8 (not_8_out, Q2);
  and and_4 (and_4_out, not_7_out, not_8_out, not_9_out);
  not not_9 (not_9_out, Q0);
  not not_10 (not_10_out, Q0);
  not not_11 (not_11_out, Q2);
  and and_5 (and_5_out, not_11_out, Q1);
  and and_6 (and_6_out, Q3, not_12_out);
  not not_12 (not_12_out, Q1);
  not not_13 (not_13_out, Q3);
  and and_7 (and_7_out, not_13_out, not_14_out);
  not not_14 (not_14_out, Q2);
  not not_15 (not_15_out, Q3);
  and and_8 (and_8_out, not_15_out, Q0);
  and and_9 (and_9_out, Q2, Q1, Q0);
  not not_16 (not_16_out, Q1);
  or or_1 (K1, not_16_out, Q2);
  not not_17 (not_17_out, Q2);
  not not_18 (not_18_out, Q0);
  not not_19 (not_19_out, Q3);
  and and_10 (and_10_out, not_19_out, Q1);
  and and_11 (and_11_out, Q3, not_20_out);
  not not_20 (not_20_out, Q1);
  or or_2 (J3, and_1_out, and_2_out, Q3);
  or or_3 (K3, and_3_out, Q2);
  or or_4 (J2, and_4_out, Q1);
  or or_5 (K2, not_10_out, and_5_out, and_6_out);
  or or_6 (J1, and_7_out, and_8_out, and_9_out);
  or or_7 (K0, not_17_out, not_18_out, and_10_out, and_11_out);

  assign J0 = 1'b1;
endmodule

module cycle_test (
  output out_1,
  output out_2,
  output out_3,
  output out_4,
  output out_5,
  output out_6,
  output out_7,
  output out_8,
  output out_9,
  output out_10,
  output out_11,
  output out_12,
  output out_13,
  output out_14,
  output out_15,
  output out_16,
  output out_17,
  output out_18,
  output out_19,
  output out_20,
  output out_21,
  output out_22,
  output out_23,
  output out_24
);

  wire clock_1_out, multicycle_1_q0, multicycle_1_q1, multicycle_1_q2, multicycle_1_q3,
       transco_nb_cyclic_1421_7seg_1_a0, transco_nb_cyclic_1421_7seg_1_a1, transco_nb_cyclic_1421_7seg_1_a2,
       transco_nb_cyclic_1421_7seg_1_a3, transco_nb_cyclic_1421_7seg_1_a4, transco_nb_cyclic_1421_7seg_1_a5,
       transco_nb_cyclic_1421_7seg_1_a6, transco_nb_cyclic_1421_7seg_1_a7, transco_nb_cyclic_1421_7seg_2_a0,
       transco_nb_cyclic_1421_7seg_2_a1, transco_nb_cyclic_1421_7seg_2_a2, transco_nb_cyclic_1421_7seg_2_a3,
       transco_nb_cyclic_1421_7seg_2_a4, transco_nb_cyclic_1421_7seg_2_a5, transco_nb_cyclic_1421_7seg_2_a6,
       transco_nb_cyclic_1421_7seg_2_a7, transco_nb_cyclic_1421_7seg_3_a0, transco_nb_cyclic_1421_7seg_3_a1,
       transco_nb_cyclic_1421_7seg_3_a2, transco_nb_cyclic_1421_7seg_3_a3, transco_nb_cyclic_1421_7seg_3_a4,
       transco_nb_cyclic_1421_7seg_3_a5, transco_nb_cyclic_1421_7seg_3_a6, transco_nb_cyclic_1421_7seg_3_a7,
       transco_nb_cyclic_1421_7seg_4_a0, transco_nb_cyclic_1421_7seg_4_a1, transco_nb_cyclic_1421_7seg_4_a2,
       transco_nb_cyclic_1421_7seg_4_a3, transco_nb_cyclic_1421_7seg_4_a4, transco_nb_cyclic_1421_7seg_4_a5,
       transco_nb_cyclic_1421_7seg_4_a6, transco_nb_cyclic_1421_7seg_4_a7, transco_nb_cyclic_1421_7seg_5_a0,
       transco_nb_cyclic_1421_7seg_5_a1, transco_nb_cyclic_1421_7seg_5_a2, transco_nb_cyclic_1421_7seg_5_a3,
       transco_nb_cyclic_1421_7seg_5_a4, transco_nb_cyclic_1421_7seg_5_a5, transco_nb_cyclic_1421_7seg_5_a6,
       transco_nb_cyclic_1421_7seg_5_a7, transco_nb_cyclic_1421_7seg_6_a0, transco_nb_cyclic_1421_7seg_6_a1,
       transco_nb_cyclic_1421_7seg_6_a2, transco_nb_cyclic_1421_7seg_6_a3, transco_nb_cyclic_1421_7seg_6_a4,
       transco_nb_cyclic_1421_7seg_6_a5, transco_nb_cyclic_1421_7seg_6_a6, transco_nb_cyclic_1421_7seg_6_a7,
       transco_nb_cyclic_1421_7seg_7_a0, transco_nb_cyclic_1421_7seg_7_a1, transco_nb_cyclic_1421_7seg_7_a2,
       transco_nb_cyclic_1421_7seg_7_a3, transco_nb_cyclic_1421_7seg_7_a4, transco_nb_cyclic_1421_7seg_7_a5,
       transco_nb_cyclic_1421_7seg_7_a6, transco_nb_cyclic_1421_7seg_7_a7;

  Clock clock_1 (.out(clock_1_out));
  multicycle multicycle_1 (
    .in_1(clock_1_out), .Q3(multicycle_1_q3), .Q2(multicycle_1_q2), .Q1(multicycle_1_q1), .Q0(multicycle_1_q0));
  transco_nb_cyclic_1421_7seg transco_nb_cyclic_1421_7seg_1 (
    .b3(multicycle_1_q3), .b2(multicycle_1_q2), .b1(multicycle_1_q1), .b0(multicycle_1_q0),
    .A7(transco_nb_cyclic_1421_7seg_1_a7), .A6(transco_nb_cyclic_1421_7seg_1_a6),
    .A5(transco_nb_cyclic_1421_7seg_1_a5), .A4(transco_nb_cyclic_1421_7seg_1_a4),
    .A3(transco_nb_cyclic_1421_7seg_1_a3), .A2(transco_nb_cyclic_1421_7seg_1_a2),
    .A1(transco_nb_cyclic_1421_7seg_1_a1), .A0(transco_nb_cyclic_1421_7seg_1_a0));
  cycle_complet_nb_1 cycle_complet_nb_1_1 (.in_1(clock_1_out), .Q3(out_1), .Q2(out_2), .Q1(out_3), .Q0(out_4));
  cycle_complet_nb_2 cycle_complet_nb_2_1 (.in_1(clock_1_out), .Q3(out_5), .Q2(out_6), .Q1(out_7), .Q0(out_8));
  cycle_complet_nb_3 cycle_complet_nb_3_1 (.in_1(clock_1_out), .Q3(out_9), .Q2(out_10), .Q1(out_11), .Q0(out_12));
  cycle_complet_nb_4 cycle_complet_nb_4_1 (.in_1(clock_1_out), .Q3(out_13), .Q2(out_14), .Q1(out_15), .Q0(out_16));
  cycle_complet_nb_5 cycle_complet_nb_5_1 (.in_1(clock_1_out), .Q3(out_17), .Q2(out_18), .Q1(out_19), .Q0(out_20));
  cycle_complet_nb_6 cycle_complet_nb_6_1 (.in_1(clock_1_out), .Q3(out_21), .Q2(out_22), .Q1(out_23), .Q0(out_24));
  transco_nb_cyclic_1421_7seg transco_nb_cyclic_1421_7seg_2 (
    .b3(out_1), .b2(out_2), .b1(out_3), .b0(out_4), .A7(transco_nb_cyclic_1421_7seg_2_a7),
    .A6(transco_nb_cyclic_1421_7seg_2_a6), .A5(transco_nb_cyclic_1421_7seg_2_a5),
    .A4(transco_nb_cyclic_1421_7seg_2_a4), .A3(transco_nb_cyclic_1421_7seg_2_a3),
    .A2(transco_nb_cyclic_1421_7seg_2_a2), .A1(transco_nb_cyclic_1421_7seg_2_a1),
    .A0(transco_nb_cyclic_1421_7seg_2_a0));
  transco_nb_cyclic_1421_7seg transco_nb_cyclic_1421_7seg_3 (
    .b3(out_5), .b2(out_6), .b1(out_7), .b0(out_8), .A7(transco_nb_cyclic_1421_7seg_3_a7),
    .A6(transco_nb_cyclic_1421_7seg_3_a6), .A5(transco_nb_cyclic_1421_7seg_3_a5),
    .A4(transco_nb_cyclic_1421_7seg_3_a4), .A3(transco_nb_cyclic_1421_7seg_3_a3),
    .A2(transco_nb_cyclic_1421_7seg_3_a2), .A1(transco_nb_cyclic_1421_7seg_3_a1),
    .A0(transco_nb_cyclic_1421_7seg_3_a0));
  transco_nb_cyclic_1421_7seg transco_nb_cyclic_1421_7seg_4 (
    .b3(out_9), .b2(out_10), .b1(out_11), .b0(out_12), .A7(transco_nb_cyclic_1421_7seg_4_a7),
    .A6(transco_nb_cyclic_1421_7seg_4_a6), .A5(transco_nb_cyclic_1421_7seg_4_a5),
    .A4(transco_nb_cyclic_1421_7seg_4_a4), .A3(transco_nb_cyclic_1421_7seg_4_a3),
    .A2(transco_nb_cyclic_1421_7seg_4_a2), .A1(transco_nb_cyclic_1421_7seg_4_a1),
    .A0(transco_nb_cyclic_1421_7seg_4_a0));
  transco_nb_cyclic_1421_7seg transco_nb_cyclic_1421_7seg_5 (
    .b3(out_13), .b2(out_14), .b1(out_15), .b0(out_16), .A7(transco_nb_cyclic_1421_7seg_5_a7),
    .A6(transco_nb_cyclic_1421_7seg_5_a6), .A5(transco_nb_cyclic_1421_7seg_5_a5),
    .A4(transco_nb_cyclic_1421_7seg_5_a4), .A3(transco_nb_cyclic_1421_7seg_5_a3),
    .A2(transco_nb_cyclic_1421_7seg_5_a2), .A1(transco_nb_cyclic_1421_7seg_5_a1),
    .A0(transco_nb_cyclic_1421_7seg_5_a0));
  transco_nb_cyclic_1421_7seg transco_nb_cyclic_1421_7seg_6 (
    .b3(out_17), .b2(out_18), .b1(out_19), .b0(out_20), .A7(transco_nb_cyclic_1421_7seg_6_a7),
    .A6(transco_nb_cyclic_1421_7seg_6_a6), .A5(transco_nb_cyclic_1421_7seg_6_a5),
    .A4(transco_nb_cyclic_1421_7seg_6_a4), .A3(transco_nb_cyclic_1421_7seg_6_a3),
    .A2(transco_nb_cyclic_1421_7seg_6_a2), .A1(transco_nb_cyclic_1421_7seg_6_a1),
    .A0(transco_nb_cyclic_1421_7seg_6_a0));
  transco_nb_cyclic_1421_7seg transco_nb_cyclic_1421_7seg_7 (
    .b3(out_21), .b2(out_22), .b1(out_23), .b0(out_24), .A7(transco_nb_cyclic_1421_7seg_7_a7),
    .A6(transco_nb_cyclic_1421_7seg_7_a6), .A5(transco_nb_cyclic_1421_7seg_7_a5),
    .A4(transco_nb_cyclic_1421_7seg_7_a4), .A3(transco_nb_cyclic_1421_7seg_7_a3),
    .A2(transco_nb_cyclic_1421_7seg_7_a2), .A1(transco_nb_cyclic_1421_7seg_7_a1),
    .A0(transco_nb_cyclic_1421_7seg_7_a0));
  _7_Segment_Display u_7_segment_display_1 (
    .g(transco_nb_cyclic_1421_7seg_1_a0), .f(transco_nb_cyclic_1421_7seg_1_a1),
    .a(transco_nb_cyclic_1421_7seg_1_a2), .b(transco_nb_cyclic_1421_7seg_1_a3),
    .e(transco_nb_cyclic_1421_7seg_1_a4), .d(transco_nb_cyclic_1421_7seg_1_a5),
    .c(transco_nb_cyclic_1421_7seg_1_a6), .dp(transco_nb_cyclic_1421_7seg_1_a7));
  _7_Segment_Display u_7_segment_display_2 (
    .g(transco_nb_cyclic_1421_7seg_2_a0), .f(transco_nb_cyclic_1421_7seg_2_a1),
    .a(transco_nb_cyclic_1421_7seg_2_a2), .b(transco_nb_cyclic_1421_7seg_2_a3),
    .e(transco_nb_cyclic_1421_7seg_2_a4), .d(transco_nb_cyclic_1421_7seg_2_a5),
    .c(transco_nb_cyclic_1421_7seg_2_a6), .dp(transco_nb_cyclic_1421_7seg_2_a7));
  _7_Segment_Display u_7_segment_display_3 (
    .g(transco_nb_cyclic_1421_7seg_3_a0), .f(transco_nb_cyclic_1421_7seg_3_a1),
    .a(transco_nb_cyclic_1421_7seg_3_a2), .b(transco_nb_cyclic_1421_7seg_3_a3),
    .e(transco_nb_cyclic_1421_7seg_3_a4), .d(transco_nb_cyclic_1421_7seg_3_a5),
    .c(transco_nb_cyclic_1421_7seg_3_a6), .dp(transco_nb_cyclic_1421_7seg_3_a7));
  _7_Segment_Display u_7_segment_display_4 (
    .g(transco_nb_cyclic_1421_7seg_4_a0), .f(transco_nb_cyclic_1421_7seg_4_a1),
    .a(transco_nb_cyclic_1421_7seg_4_a2), .b(transco_nb_cyclic_1421_7seg_4_a3),
    .e(transco_nb_cyclic_1421_7seg_4_a4), .d(transco_nb_cyclic_1421_7seg_4_a5),
    .c(transco_nb_cyclic_1421_7seg_4_a6), .dp(transco_nb_cyclic_1421_7seg_4_a7));
  _7_Segment_Display u_7_segment_display_5 (
    .g(transco_nb_cyclic_1421_7seg_5_a0), .f(transco_nb_cyclic_1421_7seg_5_a1),
    .a(transco_nb_cyclic_1421_7seg_5_a2), .b(transco_nb_cyclic_1421_7seg_5_a3),
    .e(transco_nb_cyclic_1421_7seg_5_a4), .d(transco_nb_cyclic_1421_7seg_5_a5),
    .c(transco_nb_cyclic_1421_7seg_5_a6), .dp(transco_nb_cyclic_1421_7seg_5_a7));
  _7_Segment_Display u_7_segment_display_6 (
    .g(transco_nb_cyclic_1421_7seg_6_a0), .f(transco_nb_cyclic_1421_7seg_6_a1),
    .a(transco_nb_cyclic_1421_7seg_6_a2), .b(transco_nb_cyclic_1421_7seg_6_a3),
    .e(transco_nb_cyclic_1421_7seg_6_a4), .d(transco_nb_cyclic_1421_7seg_6_a5),
    .c(transco_nb_cyclic_1421_7seg_6_a6), .dp(transco_nb_cyclic_1421_7seg_6_a7));
  _7_Segment_Display u_7_segment_display_7 (
    .g(transco_nb_cyclic_1421_7seg_7_a0), .f(transco_nb_cyclic_1421_7seg_7_a1),
    .a(transco_nb_cyclic_1421_7seg_7_a2), .b(transco_nb_cyclic_1421_7seg_7_a3),
    .e(transco_nb_cyclic_1421_7seg_7_a4), .d(transco_nb_cyclic_1421_7seg_7_a5),
    .c(transco_nb_cyclic_1421_7seg_7_a6), .dp(transco_nb_cyclic_1421_7seg_7_a7));

  // Notes on the sheet:
  //   Indexe
  //   Afficheur 1
  //   Afficheur 2
  //   Afficheur 3
  //   Afficheur 4
  //   Afficheur 5
  //   Afficheur 6
endmodule

module cycle (
  input  in_1,
  output Q3,
  output Q2,
  output Q1,
  output Q0
);

  wire finalcycle_1_j0, finalcycle_1_j1, finalcycle_1_j2, finalcycle_1_j3, finalcycle_1_k0, finalcycle_1_k1,
       finalcycle_1_k2, finalcycle_1_k3;

  J_K_Flip_Flop J3K3 (.J(finalcycle_1_j3), .clk(in_1), .K(finalcycle_1_k3), .Q(Q3));  // open: Qn, preset, en, reset
  J_K_Flip_Flop J2K2 (.J(finalcycle_1_j2), .clk(in_1), .K(finalcycle_1_k2), .Q(Q2));  // open: Qn, preset, en, reset
  J_K_Flip_Flop J1K1 (.J(finalcycle_1_j1), .clk(in_1), .K(finalcycle_1_k1), .Q(Q1));  // open: Qn, preset, en, reset
  J_K_Flip_Flop J0K0 (.J(finalcycle_1_j0), .clk(in_1), .K(finalcycle_1_k0), .Q(Q0));  // open: Qn, preset, en, reset
  finalcycle finalcycle_1 (
    .Q3(Q3), .Q2(Q2), .Q1(Q1), .Q0(Q0), .J3(finalcycle_1_j3), .K3(finalcycle_1_k3), .J2(finalcycle_1_j2),
    .K2(finalcycle_1_k2), .J1(finalcycle_1_j1), .K1(finalcycle_1_k1), .J0(finalcycle_1_j0),
    .K0(finalcycle_1_k0));
endmodule

module finalcycle (
  input  Q3,
  input  Q2,
  input  Q1,
  input  Q0,
  output J3,
  output K3,
  output J2,
  output K2,
  output J1,
  output K1,
  output J0,
  output K0
);

  wire not_3_out;

  and and_1 (J3, Q2, Q1);
  not not_1 (J2, Q1);
  not not_2 (K2, Q0);
  not not_3 (not_3_out, Q2);
  or or_1 (K1, not_3_out, Q3);

  assign J0 = Q1;
  assign J1 = Q2;
  assign K0 = Q3;
  assign K3 = 1'b1;
endmodule

module multicycle (
  input  in_1,
  output Q3,
  output Q2,
  output Q1,
  output Q0
);

  wire multiplicateurfinal_j0, multiplicateurfinal_j1, multiplicateurfinal_j2, multiplicateurfinal_j3,
       multiplicateurfinal_k0, multiplicateurfinal_k1, multiplicateurfinal_k2, multiplicateurfinal_k3;

  J_K_Flip_Flop J3K3 (
    .J(multiplicateurfinal_j3), .clk(in_1), .K(multiplicateurfinal_k3), .Q(Q3));  // open: Qn, preset, en, reset
  J_K_Flip_Flop J2K2 (
    .J(multiplicateurfinal_j2), .clk(in_1), .K(multiplicateurfinal_k2), .Q(Q2));  // open: Qn, preset, en, reset
  J_K_Flip_Flop J1K1 (
    .J(multiplicateurfinal_j1), .clk(in_1), .K(multiplicateurfinal_k1), .Q(Q1));  // open: Qn, preset, en, reset
  J_K_Flip_Flop J0K0 (
    .J(multiplicateurfinal_j0), .clk(in_1), .K(multiplicateurfinal_k0), .Q(Q0));  // open: Qn, preset, en, reset
  finalmulti multiplicateurfinal (
    .Q3(Q3), .Q2(Q2), .Q1(Q1), .Q0(Q0), .J3(multiplicateurfinal_j3), .K3(multiplicateurfinal_k3),
    .J2(multiplicateurfinal_j2), .K2(multiplicateurfinal_k2), .J1(multiplicateurfinal_j1),
    .K1(multiplicateurfinal_k1), .J0(multiplicateurfinal_j0), .K0(multiplicateurfinal_k0));
endmodule

module finalmulti (
  input  Q3,
  input  Q2,
  input  Q1,
  input  Q0,
  output J3,
  output K3,
  output J2,
  output K2,
  output J1,
  output K1,
  output J0,
  output K0
);

  wire and_1_out, and_2_out, and_3_out, not_1_out, not_2_out, not_3_out, not_4_out, not_5_out;

  not not_1 (not_1_out, Q3);
  and and_1 (and_1_out, not_1_out, not_2_out);
  not not_2 (not_2_out, Q2);
  not not_3 (not_3_out, Q3);
  and and_2 (and_2_out, not_3_out, not_4_out);
  not not_4 (not_4_out, Q1);
  and and_3 (and_3_out, Q2, Q1, Q0);
  and and_4 (J1, Q2, not_5_out);
  not not_5 (not_5_out, Q0);
  and and_5 (J0, Q2, Q1);
  or or_1 (K3, and_1_out, and_2_out, and_3_out);

  assign J2 = Q3;
  assign J3 = 1'b1;
  assign K0 = Q2;
  assign K1 = Q2;
  assign K2 = 1'b1;
endmodule

module comparateur_1 (
  input  Q3m,
  input  Q2m,
  input  Q1m,
  input  Q0m,
  input  Q3c,
  input  Q2c,
  input  Q1c,
  input  Q0c,
  output S3,
  output S2,
  output S1,
  output S0
);

  wire and_2_out, and_3_out, and_4_out, and_5_out, and_6_out, and_7_out, and_8_out, and_9_out, and_10_out,
       and_11_out, and_12_out, not_1_out, not_2_out, not_3_out, not_4_out, not_5_out, not_6_out, not_7_out,
       not_8_out, not_9_out, not_10_out, not_11_out, not_12_out, not_13_out, not_14_out, not_15_out,
       not_16_out, not_17_out, not_18_out, not_19_out, not_20_out, not_21_out, not_22_out, not_23_out,
       not_24_out, not_25_out, not_26_out, not_27_out, not_28_out, not_29_out, not_30_out, not_31_out,
       not_32_out, not_33_out, not_34_out, not_35_out;

  not not_1 (not_1_out, Q1c);
  not not_2 (not_2_out, Q3m);
  not not_3 (not_3_out, Q1m);
  not not_4 (not_4_out, Q0m);
  not not_5 (not_5_out, Q2c);
  not not_6 (not_6_out, Q1c);
  not not_7 (not_7_out, Q0c);
  not not_8 (not_8_out, Q3m);
  not not_9 (not_9_out, Q1m);
  not not_10 (not_10_out, Q0c);
  not not_11 (not_11_out, Q3m);
  not not_12 (not_12_out, Q2c);
  not not_13 (not_13_out, Q1c);
  not not_14 (not_14_out, Q1c);
  not not_15 (not_15_out, Q3m);
  not not_16 (not_16_out, Q2m);
  not not_17 (not_17_out, Q0m);
  not not_18 (not_18_out, Q1c);
  not not_19 (not_19_out, Q0c);
  not not_20 (not_20_out, Q3m);
  not not_21 (not_21_out, Q2c);
  not not_22 (not_22_out, Q1c);
  not not_23 (not_23_out, Q1c);
  not not_24 (not_24_out, Q3m);
  not not_25 (not_25_out, Q2m);
  not not_26 (not_26_out, Q1m);
  not not_27 (not_27_out, Q2c);
  not not_28 (not_28_out, Q0c);
  not not_29 (not_29_out, Q3m);
  not not_30 (not_30_out, Q1m);
  not not_31 (not_31_out, Q0c);
  not not_32 (not_32_out, Q3m);
  not not_33 (not_33_out, Q2c);
  not not_34 (not_34_out, Q1c);
  not not_35 (not_35_out, Q1c);
  and and_1 (S3, Q3m, Q2m, Q1m, Q0m, Q3c, Q2c, not_1_out, Q0c);
  and and_2 (and_2_out, not_2_out, Q2m, not_3_out, not_4_out, Q3c, not_5_out, not_6_out, not_7_out);
  and and_3 (and_3_out, not_8_out, Q2m, not_9_out, Q0m, Q3c, Q2c, Q1c, not_10_out);
  and and_4 (and_4_out, not_11_out, Q2m, Q1m, Q0m, Q3c, not_12_out, not_13_out, Q0c);
  and and_5 (and_5_out, Q3m, Q2m, Q1m, Q0m, Q3c, Q2c, not_14_out, Q0c);
  and and_6 (and_6_out, not_15_out, not_16_out, Q1m, not_17_out, Q3c, Q2c, not_18_out, not_19_out);
  and and_7 (and_7_out, not_20_out, Q2m, Q1m, Q0m, Q3c, not_21_out, not_22_out, Q0c);
  and and_8 (and_8_out, Q3m, Q2m, Q1m, Q0m, Q3c, Q2c, not_23_out, Q0c);
  and and_9 (and_9_out, not_24_out, not_25_out, not_26_out, Q0m, Q3c, not_27_out, Q1c, not_28_out);
  and and_10 (and_10_out, not_29_out, Q2m, not_30_out, Q0m, Q3c, Q2c, Q1c, not_31_out);
  and and_11 (and_11_out, not_32_out, Q2m, Q1m, Q0m, Q3c, not_33_out, not_34_out, Q0c);
  and and_12 (and_12_out, Q3m, Q2m, Q1m, Q0m, Q3c, Q2c, not_35_out, Q0c);
  or or_1 (S2, and_2_out, and_3_out, and_4_out, and_5_out);
  or or_2 (S1, and_6_out, and_7_out, and_8_out);
  or or_3 (S0, and_9_out, and_10_out, and_11_out, and_12_out);
endmodule

module comparateur_2 (
  input  Q3m,
  input  Q2m,
  input  Q1m,
  input  Q0m,
  input  Q3c,
  input  Q2c,
  input  Q1c,
  input  Q0c,
  output S3,
  output S2,
  output S1,
  output S0
);

  wire and_2_out, and_3_out, and_4_out, and_5_out, and_6_out, and_7_out, and_8_out, and_9_out, and_10_out,
       and_11_out, and_12_out, not_1_out, not_2_out, not_3_out, not_4_out, not_5_out, not_6_out, not_7_out,
       not_8_out, not_9_out, not_10_out, not_11_out, not_12_out, not_13_out, not_14_out, not_15_out,
       not_16_out, not_17_out, not_18_out, not_19_out, not_20_out, not_21_out, not_22_out, not_23_out,
       not_24_out, not_25_out, not_26_out, not_27_out, not_28_out, not_29_out, not_30_out, not_31_out,
       not_32_out, not_33_out, not_34_out, not_35_out, not_36_out;

  not not_1 (not_1_out, Q1m);
  not not_2 (not_2_out, Q0m);
  not not_3 (not_3_out, Q2m);
  not not_4 (not_4_out, Q1m);
  not not_5 (not_5_out, Q3c);
  not not_6 (not_6_out, Q1c);
  not not_7 (not_7_out, Q0c);
  not not_8 (not_8_out, Q1m);
  not not_9 (not_9_out, Q0m);
  not not_10 (not_10_out, Q1m);
  not not_11 (not_11_out, Q3c);
  not not_12 (not_12_out, Q1c);
  not not_13 (not_13_out, Q0m);
  not not_14 (not_14_out, Q3c);
  not not_15 (not_15_out, Q2m);
  not not_16 (not_16_out, Q0m);
  not not_17 (not_17_out, Q3c);
  not not_18 (not_18_out, Q2c);
  not not_19 (not_19_out, Q0c);
  not not_20 (not_20_out, Q1m);
  not not_21 (not_21_out, Q0m);
  not not_22 (not_22_out, Q0m);
  not not_23 (not_23_out, Q3c);
  not not_24 (not_24_out, Q2m);
  not not_25 (not_25_out, Q1m);
  not not_26 (not_26_out, Q0m);
  not not_27 (not_27_out, Q3c);
  not not_28 (not_28_out, Q2c);
  not not_29 (not_29_out, Q1c);
  not not_30 (not_30_out, Q1m);
  not not_31 (not_31_out, Q0m);
  not not_32 (not_32_out, Q1m);
  not not_33 (not_33_out, Q3c);
  not not_34 (not_34_out, Q1c);
  not not_35 (not_35_out, Q0m);
  not not_36 (not_36_out, Q3c);
  and and_1 (S3, Q3m, Q2m, not_1_out, not_2_out, Q3c, Q2c, Q1c, Q0c);
  and and_2 (and_2_out, Q3m, not_3_out, not_4_out, Q0m, not_5_out, Q2c, not_6_out, not_7_out);
  and and_3 (and_3_out, Q3m, Q2m, not_8_out, not_9_out, Q3c, Q2c, Q1c, Q0c);
  and and_4 (and_4_out, Q3m, Q2m, not_10_out, Q0m, not_11_out, Q2c, not_12_out, Q0c);
  and and_5 (and_5_out, Q3m, Q2m, Q1m, not_13_out, not_14_out, Q2c, Q1c, Q0c);
  and and_6 (and_6_out, Q3m, not_15_out, Q1m, not_16_out, not_17_out, not_18_out, Q1c, not_19_out);
  and and_7 (and_7_out, Q3m, Q2m, not_20_out, not_21_out, Q3c, Q2c, Q1c, Q0c);
  and and_8 (and_8_out, Q3m, Q2m, Q1m, not_22_out, not_23_out, Q2c, Q1c, Q0c);
  and and_9 (and_9_out, Q3m, not_24_out, not_25_out, not_26_out, not_27_out, not_28_out, not_29_out, Q0c);
  and and_10 (and_10_out, Q3m, Q2m, not_30_out, not_31_out, Q3c, Q2c, Q1c, Q0c);
  and and_11 (and_11_out, Q3m, Q2m, not_32_out, Q0m, not_33_out, Q2c, not_34_out, Q0c);
  and and_12 (and_12_out, Q3m, Q2m, Q1m, not_35_out, not_36_out, Q2c, Q1c, Q0c);
  or or_1 (S2, and_2_out, and_3_out, and_4_out, and_5_out);
  or or_2 (S1, and_6_out, and_7_out, and_8_out);
  or or_3 (S0, and_9_out, and_10_out, and_11_out, and_12_out);
endmodule

module comparateur_3 (
  input  Q3m,
  input  Q2m,
  input  Q1m,
  input  Q0m,
  input  Q3c,
  input  Q2c,
  input  Q1c,
  input  Q0c,
  output S3,
  output S2,
  output S1,
  output S0
);

  wire and_2_out, and_3_out, and_4_out, and_5_out, and_6_out, and_7_out, and_8_out, and_9_out, and_10_out,
       and_11_out, and_12_out, not_1_out, not_2_out, not_3_out, not_4_out, not_5_out, not_6_out, not_7_out,
       not_8_out, not_9_out, not_10_out, not_11_out, not_12_out, not_13_out, not_14_out, not_15_out,
       not_16_out, not_17_out, not_18_out, not_19_out, not_20_out, not_21_out, not_22_out, not_23_out,
       not_24_out, not_25_out, not_26_out, not_27_out, not_28_out, not_29_out, not_30_out, not_31_out,
       not_32_out, not_33_out, not_34_out, not_35_out, not_36_out, not_37_out;

  not not_1 (not_1_out, Q2m);
  not not_2 (not_2_out, Q0m);
  not not_3 (not_3_out, Q2m);
  not not_4 (not_4_out, Q0m);
  not not_5 (not_5_out, Q1m);
  not not_6 (not_6_out, Q0m);
  not not_7 (not_7_out, Q3c);
  not not_8 (not_8_out, Q1c);
  not not_9 (not_9_out, Q1m);
  not not_10 (not_10_out, Q3c);
  not not_11 (not_11_out, Q0m);
  not not_12 (not_12_out, Q3c);
  not not_13 (not_13_out, Q1c);
  not not_14 (not_14_out, Q0c);
  not not_15 (not_15_out, Q2m);
  not not_16 (not_16_out, Q1m);
  not not_17 (not_17_out, Q0m);
  not not_18 (not_18_out, Q3c);
  not not_19 (not_19_out, Q2c);
  not not_20 (not_20_out, Q0c);
  not not_21 (not_21_out, Q2m);
  not not_22 (not_22_out, Q0m);
  not not_23 (not_23_out, Q1m);
  not not_24 (not_24_out, Q3c);
  not not_25 (not_25_out, Q2m);
  not not_26 (not_26_out, Q1m);
  not not_27 (not_27_out, Q3c);
  not not_28 (not_28_out, Q2c);
  not not_29 (not_29_out, Q1c);
  not not_30 (not_30_out, Q2m);
  not not_31 (not_31_out, Q0m);
  not not_32 (not_32_out, Q1m);
  not not_33 (not_33_out, Q0m);
  not not_34 (not_34_out, Q3c);
  not not_35 (not_35_out, Q1c);
  not not_36 (not_36_out, Q1m);
  not not_37 (not_37_out, Q3c);
  and and_1 (S3, Q3m, not_1_out, Q1m, not_2_out, Q3c, Q2c, Q1c, Q0c);
  and and_2 (and_2_out, Q3m, not_3_out, Q1m, not_4_out, Q3c, Q2c, Q1c, Q0c);
  and and_3 (and_3_out, Q3m, Q2m, not_5_out, not_6_out, not_7_out, Q2c, not_8_out, Q0c);
  and and_4 (and_4_out, Q3m, Q2m, not_9_out, Q0m, not_10_out, Q2c, Q1c, Q0c);
  and and_5 (and_5_out, Q3m, Q2m, Q1m, not_11_out, not_12_out, Q2c, not_13_out, not_14_out);
  and and_6 (and_6_out, Q3m, not_15_out, not_16_out, not_17_out, not_18_out, not_19_out, Q1c, not_20_out);
  and and_7 (and_7_out, Q3m, not_21_out, Q1m, not_22_out, Q3c, Q2c, Q1c, Q0c);
  and and_8 (and_8_out, Q3m, Q2m, not_23_out, Q0m, not_24_out, Q2c, Q1c, Q0c);
  and and_9 (and_9_out, Q3m, not_25_out, not_26_out, Q0m, not_27_out, not_28_out, not_29_out, Q0c);
  and and_10 (and_10_out, Q3m, not_30_out, Q1m, not_31_out, Q3c, Q2c, Q1c, Q0c);
  and and_11 (and_11_out, Q3m, Q2m, not_32_out, not_33_out, not_34_out, Q2c, not_35_out, Q0c);
  and and_12 (and_12_out, Q3m, Q2m, not_36_out, Q0m, not_37_out, Q2c, Q1c, Q0c);
  or or_1 (S2, and_2_out, and_3_out, and_4_out, and_5_out);
  or or_2 (S1, and_6_out, and_7_out, and_8_out);
  or or_3 (S0, and_9_out, and_10_out, and_11_out, and_12_out);
endmodule

module comparateur_4 (
  input  Q3m,
  input  Q2m,
  input  Q1m,
  input  Q0m,
  input  Q3c,
  input  Q2c,
  input  Q1c,
  input  Q0c,
  output S3,
  output S2,
  output S1,
  output S0
);

  wire and_2_out, and_3_out, and_4_out, and_5_out, and_6_out, and_7_out, and_8_out, and_9_out, and_10_out,
       and_11_out, and_12_out, not_1_out, not_2_out, not_3_out, not_4_out, not_5_out, not_6_out, not_7_out,
       not_8_out, not_9_out, not_10_out, not_11_out, not_12_out, not_13_out, not_14_out, not_15_out,
       not_16_out, not_17_out, not_18_out, not_19_out, not_20_out, not_21_out, not_22_out, not_23_out,
       not_24_out, not_25_out, not_26_out, not_27_out, not_28_out, not_29_out, not_30_out, not_31_out,
       not_32_out, not_33_out, not_34_out, not_35_out, not_36_out, not_37_out, not_38_out, not_39_out,
       not_40_out, not_41_out, not_42_out;

  not not_1 (not_1_out, Q2m);
  not not_2 (not_2_out, Q1m);
  not not_3 (not_3_out, Q0m);
  not not_4 (not_4_out, Q2m);
  not not_5 (not_5_out, Q1m);
  not not_6 (not_6_out, Q0m);
  not not_7 (not_7_out, Q2m);
  not not_8 (not_8_out, Q0m);
  not not_9 (not_9_out, Q3c);
  not not_10 (not_10_out, Q1c);
  not not_11 (not_11_out, Q1m);
  not not_12 (not_12_out, Q0m);
  not not_13 (not_13_out, Q3c);
  not not_14 (not_14_out, Q1m);
  not not_15 (not_15_out, Q3c);
  not not_16 (not_16_out, Q1c);
  not not_17 (not_17_out, Q0c);
  not not_18 (not_18_out, Q2m);
  not not_19 (not_19_out, Q1m);
  not not_20 (not_20_out, Q0m);
  not not_21 (not_21_out, Q2m);
  not not_22 (not_22_out, Q1m);
  not not_23 (not_23_out, Q3c);
  not not_24 (not_24_out, Q2c);
  not not_25 (not_25_out, Q0c);
  not not_26 (not_26_out, Q1m);
  not not_27 (not_27_out, Q0m);
  not not_28 (not_28_out, Q3c);
  not not_29 (not_29_out, Q2m);
  not not_30 (not_30_out, Q1m);
  not not_31 (not_31_out, Q0m);
  not not_32 (not_32_out, Q2m);
  not not_33 (not_33_out, Q0m);
  not not_34 (not_34_out, Q3c);
  not not_35 (not_35_out, Q1c);
  not not_36 (not_36_out, Q1m);
  not not_37 (not_37_out, Q0m);
  not not_38 (not_38_out, Q3c);
  not not_39 (not_39_out, Q0m);
  not not_40 (not_40_out, Q3c);
  not not_41 (not_41_out, Q2c);
  not not_42 (not_42_out, Q1c);
  and and_1 (S3, Q3m, not_1_out, not_2_out, not_3_out, Q3c, Q2c, Q1c, Q0c);
  and and_2 (and_2_out, Q3m, not_4_out, not_5_out, not_6_out, Q3c, Q2c, Q1c, Q0c);
  and and_3 (and_3_out, Q3m, not_7_out, Q1m, not_8_out, not_9_out, Q2c, not_10_out, Q0c);
  and and_4 (and_4_out, Q3m, Q2m, not_11_out, not_12_out, not_13_out, Q2c, Q1c, Q0c);
  and and_5 (and_5_out, Q3m, Q2m, not_14_out, Q0m, not_15_out, Q2c, not_16_out, not_17_out);
  and and_6 (and_6_out, Q3m, not_18_out, not_19_out, not_20_out, Q3c, Q2c, Q1c, Q0c);
  and and_7 (and_7_out, Q3m, not_21_out, not_22_out, Q0m, not_23_out, not_24_out, Q1c, not_25_out);
  and and_8 (and_8_out, Q3m, Q2m, not_26_out, not_27_out, not_28_out, Q2c, Q1c, Q0c);
  and and_9 (and_9_out, Q3m, not_29_out, not_30_out, not_31_out, Q3c, Q2c, Q1c, Q0c);
  and and_10 (and_10_out, Q3m, not_32_out, Q1m, not_33_out, not_34_out, Q2c, not_35_out, Q0c);
  and and_11 (and_11_out, Q3m, Q2m, not_36_out, not_37_out, not_38_out, Q2c, Q1c, Q0c);
  and and_12 (and_12_out, Q3m, Q2m, Q1m, not_39_out, not_40_out, not_41_out, not_42_out, Q0c);
  or or_1 (S2, and_2_out, and_3_out, and_4_out, and_5_out);
  or or_2 (S1, and_6_out, and_7_out, and_8_out);
  or or_3 (S0, and_9_out, and_10_out, and_11_out, and_12_out);
endmodule

module comparateur_5 (
  input  Q3m,
  input  Q2m,
  input  Q1m,
  input  Q0m,
  input  Q3c,
  input  Q2c,
  input  Q1c,
  input  Q0c,
  output S3,
  output S2,
  output S1,
  output S0
);

  wire and_2_out, and_3_out, and_4_out, and_5_out, and_6_out, and_7_out, and_8_out, and_9_out, and_10_out,
       and_11_out, and_12_out, not_1_out, not_2_out, not_3_out, not_4_out, not_5_out, not_6_out, not_7_out,
       not_8_out, not_9_out, not_10_out, not_11_out, not_12_out, not_13_out, not_14_out, not_15_out,
       not_16_out, not_17_out, not_18_out, not_19_out, not_20_out, not_21_out, not_22_out, not_23_out,
       not_24_out, not_25_out, not_26_out, not_27_out, not_28_out, not_29_out, not_30_out, not_31_out,
       not_32_out, not_33_out, not_34_out, not_35_out, not_36_out, not_37_out, not_38_out, not_39_out,
       not_40_out;

  not not_1 (not_1_out, Q2m);
  not not_2 (not_2_out, Q1m);
  not not_3 (not_3_out, Q2m);
  not not_4 (not_4_out, Q1m);
  not not_5 (not_5_out, Q0m);
  not not_6 (not_6_out, Q3c);
  not not_7 (not_7_out, Q1c);
  not not_8 (not_8_out, Q2m);
  not not_9 (not_9_out, Q1m);
  not not_10 (not_10_out, Q2m);
  not not_11 (not_11_out, Q0m);
  not not_12 (not_12_out, Q3c);
  not not_13 (not_13_out, Q1m);
  not not_14 (not_14_out, Q0m);
  not not_15 (not_15_out, Q3c);
  not not_16 (not_16_out, Q1c);
  not not_17 (not_17_out, Q0c);
  not not_18 (not_18_out, Q2m);
  not not_19 (not_19_out, Q1m);
  not not_20 (not_20_out, Q2m);
  not not_21 (not_21_out, Q0m);
  not not_22 (not_22_out, Q3c);
  not not_23 (not_23_out, Q0m);
  not not_24 (not_24_out, Q3c);
  not not_25 (not_25_out, Q2c);
  not not_26 (not_26_out, Q0c);
  not not_27 (not_27_out, Q2m);
  not not_28 (not_28_out, Q1m);
  not not_29 (not_29_out, Q0m);
  not not_30 (not_30_out, Q3c);
  not not_31 (not_31_out, Q1c);
  not not_32 (not_32_out, Q2m);
  not not_33 (not_33_out, Q1m);
  not not_34 (not_34_out, Q2m);
  not not_35 (not_35_out, Q0m);
  not not_36 (not_36_out, Q3c);
  not not_37 (not_37_out, Q1m);
  not not_38 (not_38_out, Q3c);
  not not_39 (not_39_out, Q2c);
  not not_40 (not_40_out, Q1c);
  and and_1 (S3, Q3m, not_1_out, not_2_out, Q0m, Q3c, Q2c, Q1c, Q0c);
  and and_2 (and_2_out, Q3m, not_3_out, not_4_out, not_5_out, not_6_out, Q2c, not_7_out, Q0c);
  and and_3 (and_3_out, Q3m, not_8_out, not_9_out, Q0m, Q3c, Q2c, Q1c, Q0c);
  and and_4 (and_4_out, Q3m, not_10_out, Q1m, not_11_out, not_12_out, Q2c, Q1c, Q0c);
  and and_5 (and_5_out, Q3m, Q2m, not_13_out, not_14_out, not_15_out, Q2c, not_16_out, not_17_out);
  and and_6 (and_6_out, Q3m, not_18_out, not_19_out, Q0m, Q3c, Q2c, Q1c, Q0c);
  and and_7 (and_7_out, Q3m, not_20_out, Q1m, not_21_out, not_22_out, Q2c, Q1c, Q0c);
  and and_8 (and_8_out, Q3m, Q2m, Q1m, not_23_out, not_24_out, not_25_out, Q1c, not_26_out);
  and and_9 (and_9_out, Q3m, not_27_out, not_28_out, not_29_out, not_30_out, Q2c, not_31_out, Q0c);
  and and_10 (and_10_out, Q3m, not_32_out, not_33_out, Q0m, Q3c, Q2c, Q1c, Q0c);
  and and_11 (and_11_out, Q3m, not_34_out, Q1m, not_35_out, not_36_out, Q2c, Q1c, Q0c);
  and and_12 (and_12_out, Q3m, Q2m, not_37_out, Q0m, not_38_out, not_39_out, not_40_out, Q0c);
  or or_1 (S2, and_2_out, and_3_out, and_4_out, and_5_out);
  or or_2 (S1, and_6_out, and_7_out, and_8_out);
  or or_3 (S0, and_9_out, and_10_out, and_11_out, and_12_out);
endmodule
module comparateur_6 (
  input  Q3m,
  input  Q2m,
  input  Q1m,
  input  Q0m,
  input  Q3c,
  input  Q2c,
  input  Q1c,
  input  Q0c,
  output S3,
  output S2,
  output S1,
  output S0
);

  wire and_2_out, and_3_out, and_4_out, and_5_out, and_6_out, and_7_out, and_8_out, and_9_out, and_10_out,
       and_11_out, and_12_out, not_1_out, not_2_out, not_3_out, not_4_out, not_5_out, not_6_out, not_7_out,
       not_8_out, not_9_out, not_10_out, not_11_out, not_12_out, not_13_out, not_14_out, not_15_out,
       not_16_out, not_17_out, not_18_out, not_19_out, not_20_out, not_21_out, not_22_out, not_23_out,
       not_24_out, not_25_out, not_26_out, not_27_out, not_28_out, not_29_out, not_30_out, not_31_out,
       not_32_out, not_33_out, not_34_out, not_35_out, not_36_out, not_37_out, not_38_out;

  not not_1 (not_1_out, Q0m);
  not not_2 (not_2_out, Q2m);
  not not_3 (not_3_out, Q1m);
  not not_4 (not_4_out, Q0m);
  not not_5 (not_5_out, Q3c);
  not not_6 (not_6_out, Q2m);
  not not_7 (not_7_out, Q1m);
  not not_8 (not_8_out, Q3c);
  not not_9 (not_9_out, Q1c);
  not not_10 (not_10_out, Q2m);
  not not_11 (not_11_out, Q0m);
  not not_12 (not_12_out, Q3c);
  not not_13 (not_13_out, Q1c);
  not not_14 (not_14_out, Q0c);
  not not_15 (not_15_out, Q0m);
  not not_16 (not_16_out, Q2m);
  not not_17 (not_17_out, Q1m);
  not not_18 (not_18_out, Q0m);
  not not_19 (not_19_out, Q3c);
  not not_20 (not_20_out, Q1m);
  not not_21 (not_21_out, Q3c);
  not not_22 (not_22_out, Q2c);
  not not_23 (not_23_out, Q0c);
  not not_24 (not_24_out, Q0m);
  not not_25 (not_25_out, Q2m);
  not not_26 (not_26_out, Q1m);
  not not_27 (not_27_out, Q0m);
  not not_28 (not_28_out, Q3c);
  not not_29 (not_29_out, Q2m);
  not not_30 (not_30_out, Q1m);
  not not_31 (not_31_out, Q3c);
  not not_32 (not_32_out, Q1c);
  not not_33 (not_33_out, Q1m);
  not not_34 (not_34_out, Q0m);
  not not_35 (not_35_out, Q3c);
  not not_36 (not_36_out, Q2c);
  not not_37 (not_37_out, Q1c);
  not not_38 (not_38_out, Q0m);
  and and_1 (S3, Q3m, Q2m, Q1m, not_1_out, Q3c, Q2c, Q1c, Q0c);
  and and_2 (and_2_out, Q3m, not_2_out, not_3_out, not_4_out, not_5_out, Q2c, Q1c, Q0c);
  and and_3 (and_3_out, Q3m, not_6_out, not_7_out, Q0m, not_8_out, Q2c, not_9_out, Q0c);
  and and_4 (and_4_out, Q3m, not_10_out, Q1m, not_11_out, not_12_out, Q2c, not_13_out, not_14_out);
  and and_5 (and_5_out, Q3m, Q2m, Q1m, not_15_out, Q3c, Q2c, Q1c, Q0c);
  and and_6 (and_6_out, Q3m, not_16_out, not_17_out, not_18_out, not_19_out, Q2c, Q1c, Q0c);
  and and_7 (and_7_out, Q3m, Q2m, not_20_out, Q0m, not_21_out, not_22_out, Q1c, not_23_out);
  and and_8 (and_8_out, Q3m, Q2m, Q1m, not_24_out, Q3c, Q2c, Q1c, Q0c);
  and and_9 (and_9_out, Q3m, not_25_out, not_26_out, not_27_out, not_28_out, Q2c, Q1c, Q0c);
  and and_10 (and_10_out, Q3m, not_29_out, not_30_out, Q0m, not_31_out, Q2c, not_32_out, Q0c);
  and and_11 (and_11_out, Q3m, Q2m, not_33_out, not_34_out, not_35_out, not_36_out, not_37_out, Q0c);
  and and_12 (and_12_out, Q3m, Q2m, Q1m, not_38_out, Q3c, Q2c, Q1c, Q0c);
  or or_1 (S2, and_2_out, and_3_out, and_4_out, and_5_out);
  or or_2 (S1, and_6_out, and_7_out, and_8_out);
  or or_3 (S0, and_9_out, and_10_out, and_11_out, and_12_out);
endmodule

module affres_mult (
  input  A,
  input  B,
  input  C,
  input  D,
  output a7,
  output a6,
  output a5,
  output a4,
  output a3,
  output a2,
  output a1,
  output a0
);

  wire and_1_out, and_2_out, and_3_out, and_4_out, and_5_out, and_6_out, and_7_out, and_8_out, and_9_out,
       and_10_out, and_12_out, and_13_out, and_14_out, not_1_out, not_2_out, not_3_out, not_4_out, not_5_out,
       not_6_out, not_7_out, not_8_out, not_9_out, not_10_out, not_11_out, not_12_out, not_13_out,
       not_14_out, not_15_out, not_16_out, not_17_out, not_18_out, not_19_out;

  not not_1 (not_1_out, C);
  and and_1 (and_1_out, B, not_1_out, not_2_out);
  not not_2 (not_2_out, D);
  and and_2 (and_2_out, A, not_3_out);
  not not_3 (not_3_out, C);
  and and_3 (and_3_out, A, not_4_out);
  not not_4 (not_4_out, D);
  not not_5 (not_5_out, B);
  and and_4 (and_4_out, A, not_5_out, not_6_out);
  not not_6 (not_6_out, C);
  and and_5 (and_5_out, A, not_7_out, D);
  not not_7 (not_7_out, C);
  and and_6 (and_6_out, A, C, not_8_out);
  not not_8 (not_8_out, D);
  not not_9 (not_9_out, A);
  not not_10 (not_10_out, B);
  and and_7 (and_7_out, not_10_out, C);
  and and_8 (and_8_out, B, not_11_out);
  not not_11 (not_11_out, C);
  not not_12 (not_12_out, A);
  and and_9 (and_9_out, C, D);
  and and_10 (and_10_out, B, not_13_out);
  not not_13 (not_13_out, C);
  and and_11 (a3, A, not_14_out);
  not not_14 (not_14_out, D);
  not not_15 (not_15_out, A);
  not not_16 (not_16_out, B);
  and and_12 (and_12_out, not_16_out, C);
  and and_13 (and_13_out, B, not_17_out);
  not not_17 (not_17_out, C);
  not not_18 (not_18_out, A);
  and and_14 (and_14_out, B, C);
  not not_19 (not_19_out, A);
  or or_1 (a7, and_1_out, and_2_out, and_3_out);
  or or_2 (a6, and_4_out, and_5_out, and_6_out);
  or or_3 (a5, not_9_out, D, and_7_out, and_8_out);
  or or_4 (a4, not_12_out, and_9_out, and_10_out);
  or or_5 (a2, not_15_out, D, and_12_out, and_13_out);
  or or_6 (a1, not_18_out, D, and_14_out);
  or or_7 (a0, not_19_out, D, C, B);
endmodule

module tickblocker (
  input  Q3,
  input  Q2,
  input  Q1,
  input  Q0,
  output S
);

  or or_1 (S, Q0, Q1, Q2, Q3);
endmodule
